// Logisim project 16bitCPU_Delali.circ as structural Verilog
module singleBitFullAdder (
  input  A,
  input  B,
  input  Cin,
  output sum,
  output carry
);

  wire and_1_out, and_2_out, and_3_out, xor_1_out;

  xor xor_1 (xor_1_out, A, B);
  and and_1 (and_1_out, A, B);
  and and_2 (and_2_out, B, Cin);
  and and_3 (and_3_out, A, Cin);
  xor xor_2 (sum, xor_1_out, Cin);
  or or_1 (carry, and_1_out, and_2_out, and_3_out);

  // Notes on the sheet:
  //   single bit full adder
endmodule

module fullAdder2Bit (
  input  [1:0] A,
  input  cin,
  input  [1:0] B,
  output [1:0] sum,
  output carry
);

  wire singlebitfulladder_1_carry;

  singleBitFullAdder singlebitfulladder_1 (
    .A(A[0]), .B(B[0]), .Cin(cin), .sum(sum[0]), .carry(singlebitfulladder_1_carry));
  singleBitFullAdder singlebitfulladder_2 (
    .A(A[1]), .B(B[1]), .Cin(singlebitfulladder_1_carry), .sum(sum[1]), .carry(carry));
endmodule

module addsub2bit (
  input  ctrl,
  input  [1:0] A,
  input  [1:0] B,
  output [1:0] sum_or_difference,
  output discarded_overflow
);

  wire singlebitfulladder_1_carry, xor_1_out, xor_2_out;

  xor xor_1 (xor_1_out, B[1], ctrl);
  xor xor_2 (xor_2_out, ctrl, B[0]);
  singleBitFullAdder singlebitfulladder_1 (
    .A(A[0]), .B(xor_2_out), .Cin(ctrl), .sum(sum_or_difference[0]), .carry(singlebitfulladder_1_carry));
  singleBitFullAdder singlebitfulladder_2 (
    .A(A[1]), .B(xor_1_out), .Cin(singlebitfulladder_1_carry), .sum(sum_or_difference[1]),
    .carry(discarded_overflow));

  // Notes on the sheet:
  //   add sub 2 bit
  //   2's complemnet of B
endmodule

module fulladder8bit (
  input  [7:0] A,
  input  initial_cin,
  input  [7:0] B,
  output [7:0] sum,
  output carry
);

  wire singlebitfulladder_1_carry, singlebitfulladder_2_carry, singlebitfulladder_3_carry,
       singlebitfulladder_4_carry, singlebitfulladder_5_carry, singlebitfulladder_6_carry,
       singlebitfulladder_7_carry;

  singleBitFullAdder singlebitfulladder_1 (
    .A(A[0]), .B(B[0]), .Cin(initial_cin), .sum(sum[0]), .carry(singlebitfulladder_1_carry));
  singleBitFullAdder singlebitfulladder_2 (
    .A(A[1]), .B(B[1]), .Cin(singlebitfulladder_1_carry), .sum(sum[1]), .carry(singlebitfulladder_2_carry));
  singleBitFullAdder singlebitfulladder_3 (
    .A(A[2]), .B(B[2]), .Cin(singlebitfulladder_2_carry), .sum(sum[2]), .carry(singlebitfulladder_3_carry));
  singleBitFullAdder singlebitfulladder_4 (
    .A(A[3]), .B(B[3]), .Cin(singlebitfulladder_3_carry), .sum(sum[3]), .carry(singlebitfulladder_4_carry));
  singleBitFullAdder singlebitfulladder_5 (
    .A(A[4]), .B(B[4]), .Cin(singlebitfulladder_4_carry), .sum(sum[4]), .carry(singlebitfulladder_5_carry));
  singleBitFullAdder singlebitfulladder_6 (
    .A(A[5]), .B(B[5]), .Cin(singlebitfulladder_5_carry), .sum(sum[5]), .carry(singlebitfulladder_6_carry));
  singleBitFullAdder singlebitfulladder_7 (
    .A(A[6]), .B(B[6]), .Cin(singlebitfulladder_6_carry), .sum(sum[6]), .carry(singlebitfulladder_7_carry));
  singleBitFullAdder singlebitfulladder_8 (
    .A(A[7]), .B(B[7]), .Cin(singlebitfulladder_7_carry), .sum(sum[7]), .carry(carry));

  // Notes on the sheet:
  //   full 8 bit adder
endmodule

module addsub8bit (
  input  control,
  input  [7:0] A,
  input  cin,
  input  [7:0] B,
  output [7:0] sum,
  output carry,
  output overflow
);

  wire singlebitfulladder_1_carry, singlebitfulladder_2_carry, singlebitfulladder_3_carry,
       singlebitfulladder_4_carry, singlebitfulladder_5_carry, singlebitfulladder_6_carry,
       singlebitfulladder_7_carry, xor_1_out, xor_2_out, xor_3_out, xor_4_out, xor_5_out, xor_6_out,
       xor_7_out, xor_8_out;

  xor xor_1 (xor_1_out, control, B[1]);
  xor xor_2 (xor_2_out, control, B[2]);
  xor xor_3 (xor_3_out, control, B[3]);
  xor xor_4 (xor_4_out, B[4], control);
  xor xor_5 (xor_5_out, B[5], control);
  xor xor_6 (xor_6_out, B[6], control);
  xor xor_7 (xor_7_out, B[7], control);
  xor xor_8 (xor_8_out, control, B[0]);
  singleBitFullAdder singlebitfulladder_1 (
    .A(A[0]), .B(xor_8_out), .Cin(cin), .sum(sum[0]), .carry(singlebitfulladder_1_carry));
  singleBitFullAdder singlebitfulladder_2 (
    .A(A[1]), .B(xor_1_out), .Cin(singlebitfulladder_1_carry), .sum(sum[1]),
    .carry(singlebitfulladder_2_carry));
  singleBitFullAdder singlebitfulladder_3 (
    .A(A[2]), .B(xor_2_out), .Cin(singlebitfulladder_2_carry), .sum(sum[2]),
    .carry(singlebitfulladder_3_carry));
  singleBitFullAdder singlebitfulladder_4 (
    .A(A[3]), .B(xor_3_out), .Cin(singlebitfulladder_3_carry), .sum(sum[3]),
    .carry(singlebitfulladder_4_carry));
  singleBitFullAdder singlebitfulladder_5 (
    .A(A[4]), .B(xor_4_out), .Cin(singlebitfulladder_4_carry), .sum(sum[4]),
    .carry(singlebitfulladder_5_carry));
  singleBitFullAdder singlebitfulladder_6 (
    .A(A[5]), .B(xor_5_out), .Cin(singlebitfulladder_5_carry), .sum(sum[5]),
    .carry(singlebitfulladder_6_carry));
  singleBitFullAdder singlebitfulladder_7 (
    .A(A[6]), .B(xor_6_out), .Cin(singlebitfulladder_6_carry), .sum(sum[6]),
    .carry(singlebitfulladder_7_carry));
  singleBitFullAdder singlebitfulladder_8 (
    .A(A[7]), .B(xor_7_out), .Cin(singlebitfulladder_7_carry), .sum(sum[7]), .carry(carry));
  xor xor_9 (overflow, singlebitfulladder_7_carry, carry);
endmodule

module AU (
  input  ctrl,
  input  [7:0] A,
  input  [7:0] B,
  input  [1:0] selector,
  output cout,
  output [7:0] result
);

  wire [7:0] addsub8bit_1_sum, divider_1_out, multiplier_1_out;

  Multiplier multiplier_1 (.a(A), .b(B), .out(multiplier_1_out));  // open: cin, cout
  Divider divider_1 (.a(A), .b(B), .out(divider_1_out));  // open: upper, rem
  addsub8bit addsub8bit_1 (.control(ctrl), .A(A), .B(B), .sum(addsub8bit_1_sum), .carry(cout));  // open: cin, overflow
  Multiplexer #(.select(2), .width(8)) multiplexer_1 (
    .in0(addsub8bit_1_sum), .in1(multiplier_1_out), .in2(divider_1_out), .out(result), .sel(selector));  // open: in3

  // Notes on the sheet:
  //   Arithmetic Unit
endmodule

module LU (
  input  [7:0] A,
  input  [7:0] B,
  input  [1:0] in_3,
  output out_4
);

  wire comparator_1_eq, comparator_1_gt, comparator_1_lt;

  Comparator #(.mode("unsigned")) comparator_1 (
    .a(A), .b(B), .gt(comparator_1_gt), .eq(comparator_1_eq), .lt(comparator_1_lt));
  Multiplexer #(.select(2)) multiplexer_1 (
    .in0(comparator_1_gt), .in1(comparator_1_eq), .in2(comparator_1_lt), .out(out_4), .sel(in_3));  // open: in3
endmodule

module MemoryCell (
  input  WE,
  input  Din,
  input  Clock,
  input  OE,
  input  reset,
  output Dout,
  output stored_data
);

  wire and_1_out, and_2_out, not_1_out, or_1_out;

  not not_1 (not_1_out, WE);
  and and_1 (and_1_out, stored_data, not_1_out);
  and and_2 (and_2_out, WE, Din);
  or or_1 (or_1_out, and_1_out, and_2_out);
  D_Flip_Flop d_ff_1 (.D(or_1_out), .clk(Clock), .Q(stored_data), .reset(reset));  // open: Qn, preset
  assign Dout = OE ? stored_data : 1'bz;  // Controlled_Buffer controlled_buffer_1

  // Notes on the sheet:
  //   Memory Cell
  //   controlled_buffer
endmodule

module LU_ext (
  input  [7:0] A,
  input  [7:0] B,
  input  [2:0] selector,
  output result
);

  wire comparator_1_eq, comparator_1_gt, comparator_1_lt, not_1_out, or_1_out, or_2_out;

  Comparator #(.mode("unsigned")) comparator_1 (
    .a(A), .b(B), .gt(comparator_1_gt), .eq(comparator_1_eq), .lt(comparator_1_lt));
  or or_1 (or_1_out, comparator_1_eq, comparator_1_gt);
  not not_1 (not_1_out, comparator_1_eq);
  or or_2 (or_2_out, comparator_1_eq, comparator_1_lt);
  Multiplexer #(.select(3)) multiplexer_1 (
    .in0(or_1_out), .in1(comparator_1_gt), .in2(comparator_1_eq), .in3(comparator_1_lt), .in4(or_2_out),
    .in5(not_1_out), .out(result), .sel(selector));  // open: in6, in7

  // Notes on the sheet:
  //   comparator
  //   >=
  //   >
  //   =
  //   <=
  //   <
  //   !=
endmodule

module ALU (
  input  control,
  input  [7:0] A,
  input  [7:0] B,
  input  [1:0] AU_Sel,
  input  [2:0] LU_Sel,
  input  OE,
  output cout,
  output [7:0] AU_Dout,
  output [7:0] AU_result,
  output LU_result
);

  AU au_1 (.ctrl(control), .A(A), .B(B), .selector(AU_Sel), .cout(cout), .result(AU_result));
  LU_ext lu_ext_1 (.A(A), .B(B), .selector(LU_Sel), .result(LU_result));
  assign AU_Dout = OE ? AU_result : 8'bz;  // Controlled_Buffer controlled_buffer_1

  // Notes on the sheet:
  //   selector
  //   ALU
  //   selector
  //   result
  //   result
endmodule

module multiplier2bit (
  input  [1:0] A,
  input  [1:0] B,
  output [3:0] product
);

  wire a0b1_out, a1b0_out, a1b1_out, singlebitfulladder_1_carry;

  and a0b0 (product[0], A[0], B[0]);
  and a1b0 (a1b0_out, A[1], B[0]);
  and a0b1 (a0b1_out, A[0], B[1]);
  and a1b1 (a1b1_out, A[1], B[1]);
  singleBitFullAdder singlebitfulladder_1 (
    .A(a1b0_out), .B(a0b1_out), .sum(product[1]), .carry(singlebitfulladder_1_carry));  // open: Cin
  singleBitFullAdder singlebitfulladder_2 (
    .B(a1b1_out), .Cin(singlebitfulladder_1_carry), .sum(product[2]), .carry(product[3]));  // open: A

  // Notes on the sheet:
  //   2 bit multiplier
endmodule

module multiplier3bit (
  input  [2:0] A,
  input  [2:0] B,
  output [5:0] product
);

  wire a0b1_out, a0b2_out, a1b0_a0b1_carry, a1b0_out, a1b1_out, a1b2_out, a2b0_a1b1_carry, a2b0_a1b1_sum,
       a2b0_out, a2b1_a1b2_carry, a2b1_out, a2b2_out, prevSum_a0b2_carry;

  and a0b0 (product[0], A[0], B[0]);
  and a1b0 (a1b0_out, A[1], B[0]);
  and a0b1 (a0b1_out, A[0], B[1]);
  and a2b0 (a2b0_out, A[2], B[0]);
  and a1b1 (a1b1_out, A[1], B[1]);
  and a0b2 (a0b2_out, A[0], B[2]);
  and a2b1 (a2b1_out, A[2], B[1]);
  and a1b2 (a1b2_out, A[1], B[2]);
  and a2b2 (a2b2_out, A[2], B[2]);
  singleBitFullAdder a1b0_a0b1 (.A(a1b0_out), .B(a0b1_out), .sum(product[1]), .carry(a1b0_a0b1_carry));  // open: Cin
  singleBitFullAdder a2b0_a1b1 (
    .A(a2b0_out), .B(a1b1_out), .Cin(a1b0_a0b1_carry), .sum(a2b0_a1b1_sum), .carry(a2b0_a1b1_carry));
  singleBitFullAdder prevSum_a0b2 (
    .A(a2b0_a1b1_sum), .B(a0b2_out), .Cin(a2b0_a1b1_carry), .sum(product[2]), .carry(prevSum_a0b2_carry));
  singleBitFullAdder a2b1_a1b2 (
    .A(a2b1_out), .B(a1b2_out), .Cin(prevSum_a0b2_carry), .sum(product[3]), .carry(a2b1_a1b2_carry));
  singleBitFullAdder singlebitfulladder_1 (
    .B(a2b2_out), .Cin(a2b1_a1b2_carry), .sum(product[4]), .carry(product[5]));  // open: A

  // Notes on the sheet:
  //   3 bit multiplier
endmodule

module reg4bits (
  input  WE,
  input  [3:0] DIN,
  input  CLOCK,
  input  OE,
  input  Reset,
  output [3:0] DOUT,
  output [3:0] stored_data
);

  MemoryCell memorycell_1 (
    .WE(WE), .Din(DIN[0]), .Clock(CLOCK), .OE(OE), .reset(Reset), .Dout(DOUT[0]), .stored_data(stored_data[0]));
  MemoryCell memorycell_2 (
    .WE(WE), .Din(DIN[1]), .Clock(CLOCK), .OE(OE), .reset(Reset), .Dout(DOUT[1]), .stored_data(stored_data[1]));
  MemoryCell memorycell_3 (
    .WE(WE), .Din(DIN[2]), .Clock(CLOCK), .OE(OE), .reset(Reset), .Dout(DOUT[2]), .stored_data(stored_data[2]));
  MemoryCell memorycell_4 (
    .WE(WE), .Din(DIN[3]), .Clock(CLOCK), .OE(OE), .reset(Reset), .Dout(DOUT[3]), .stored_data(stored_data[3]));

  // Notes on the sheet:
  //   MAR_4_bit
endmodule

module reg8bits (
  input  WE,
  input  [7:0] DIN,
  input  CLOCK,
  input  OE,
  input  Reset,
  output [7:0] DOUT,
  output [7:0] stored_data
);

  reg4bits reg4bits_1 (
    .WE(WE), .DIN(DIN[3:0]), .CLOCK(CLOCK), .OE(OE), .Reset(Reset), .DOUT(DOUT[3:0]),
    .stored_data(stored_data[3:0]));
  reg4bits reg4bits_2 (
    .WE(WE), .DIN(DIN[7:4]), .CLOCK(CLOCK), .OE(OE), .Reset(Reset), .DOUT(DOUT[7:4]),
    .stored_data(stored_data[7:4]));

  // Notes on the sheet:
  //   MAR_8_bit
endmodule

module shiftReg6bit (
  input  SW,
  input  [5:0] Pl_in,
  output Sout
);

  wire and_1_out, and_2_out, and_3_out, and_4_out, and_5_out, and_6_out, and_7_out, and_8_out, and_9_out,
       and_10_out, and_11_out, clock_1_out, d_ff_1_q, d_ff_2_q, d_ff_3_q, d_ff_4_q, d_ff_5_q, not_1_out,
       or_1_out, or_2_out, or_3_out, or_4_out, or_5_out;

  Clock clock_1 (.out(clock_1_out));
  not not_1 (not_1_out, SW);
  and and_1 (and_1_out, Pl_in[0], not_1_out);
  D_Flip_Flop d_ff_1 (.D(and_1_out), .clk(clock_1_out), .Q(d_ff_1_q));  // open: Qn, preset, reset
  and and_2 (and_2_out, not_1_out, Pl_in[1]);
  and and_3 (and_3_out, d_ff_1_q, SW);
  D_Flip_Flop d_ff_2 (.D(or_1_out), .clk(clock_1_out), .Q(d_ff_2_q));  // open: Qn, preset, reset
  or or_1 (or_1_out, and_2_out, and_3_out);
  and and_4 (and_4_out, not_1_out, Pl_in[2]);
  and and_5 (and_5_out, d_ff_2_q, SW);
  D_Flip_Flop d_ff_3 (.D(or_2_out), .clk(clock_1_out), .Q(d_ff_3_q));  // open: Qn, preset, reset
  or or_2 (or_2_out, and_4_out, and_5_out);
  and and_6 (and_6_out, not_1_out, Pl_in[3]);
  or or_3 (or_3_out, and_6_out, and_7_out);
  and and_7 (and_7_out, d_ff_3_q, SW);
  D_Flip_Flop d_ff_4 (.D(or_3_out), .clk(clock_1_out), .Q(d_ff_4_q));  // open: Qn, preset, reset
  and and_8 (and_8_out, not_1_out, Pl_in[4]);
  and and_9 (and_9_out, d_ff_4_q, SW);
  or or_4 (or_4_out, and_8_out, and_9_out);
  D_Flip_Flop d_ff_5 (.D(or_4_out), .clk(clock_1_out), .Q(d_ff_5_q));  // open: Qn, preset, reset
  and and_10 (and_10_out, not_1_out, Pl_in[5]);
  and and_11 (and_11_out, d_ff_5_q, SW);
  D_Flip_Flop d_ff_6 (.D(or_5_out), .clk(clock_1_out), .Q(Sout));  // open: Qn, preset, reset
  or or_5 (or_5_out, and_10_out, and_11_out);
endmodule

module Datapath (
  input  in_1,
  input  [3:0] oe_test,
  input  [7:0] Test_data,
  input  OE,
  input  in_5,
  input  in_6,
  input  Ctrl,
  input  [1:0] AU_Selectors,
  input  [2:0] LU_Selectors,
  input  in_10,
  output [3:0] MAR_Content,
  output [3:0] counter_content,
  output [7:0] IR_Content,
  output [7:0] MBR_Content,
  output [7:0] out_15,
  output out_16,
  output [7:0] out_17,
  output [7:0] AU_Result,
  output LU_Result,
  output [2:0] sc_content,
  output [7:0] Reg_B_Content,
  output [31:0] out_22
);

  wire clock_1_out, Control_Unit_c0, Control_Unit_c1, Control_Unit_c2, Control_Unit_c3, Control_Unit_c4,
       Control_Unit_c5, Control_Unit_c6, Control_Unit_c7, Control_Unit_c8, Control_Unit_c9, Control_Unit_c10,
       Control_Unit_c11, Control_Unit_c12, Control_Unit_c13, Control_Unit_c14, Control_Unit_c15;
  wire [2:0] undriven;
  wire [3:0] bitselector_2_out, controlled_buffer_1_out, reg4bits_1_dout;
  wire [7:0] alu_1_au_dout, bit_extender_1_out, bit_extender_2_out, ram_1_dout, reg8bits_1_dout;
  wire [31:0] decimal_decoder_1_dout, decimal_decoder_2_dout, decimal_decoder_3_dout, decimal_decoder_4_dout;

  Decimal_Decoder decimal_decoder_1 (.Din(out_15), .Dout(decimal_decoder_1_dout));
  _7_Segment_Display u_7_segment_display_1 (
    .g(decimal_decoder_1_dout[15]), .f(decimal_decoder_1_dout[14]), .a(decimal_decoder_1_dout[13]),
    .b(decimal_decoder_1_dout[12]), .e(decimal_decoder_1_dout[31]), .d(decimal_decoder_1_dout[30]),
    .c(decimal_decoder_1_dout[29]), .dp(decimal_decoder_1_dout[28]));
  _7_Segment_Display u_7_segment_display_2 (
    .g(decimal_decoder_1_dout[11]), .f(decimal_decoder_1_dout[10]), .a(decimal_decoder_1_dout[9]),
    .b(decimal_decoder_1_dout[8]), .e(decimal_decoder_1_dout[27]), .d(decimal_decoder_1_dout[26]),
    .c(decimal_decoder_1_dout[25]), .dp(decimal_decoder_1_dout[24]));
  _7_Segment_Display u_7_segment_display_3 (
    .g(decimal_decoder_1_dout[7]), .f(decimal_decoder_1_dout[6]), .a(decimal_decoder_1_dout[5]),
    .b(decimal_decoder_1_dout[4]), .e(decimal_decoder_1_dout[23]), .d(decimal_decoder_1_dout[22]),
    .c(decimal_decoder_1_dout[21]), .dp(decimal_decoder_1_dout[20]));
  _7_Segment_Display u_7_segment_display_4 (
    .g(decimal_decoder_1_dout[3]), .f(decimal_decoder_1_dout[2]), .a(decimal_decoder_1_dout[1]),
    .b(decimal_decoder_1_dout[0]), .e(decimal_decoder_1_dout[19]), .d(decimal_decoder_1_dout[18]),
    .c(decimal_decoder_1_dout[17]), .dp(decimal_decoder_1_dout[16]));
  Clock clock_1 (.out(clock_1_out));
  Counter #(.max('h3), .width(4)) Program_counter (
    .count(Control_Unit_c1), .clk(clock_1_out), .D(controlled_buffer_1_out), .Q(counter_content));  // open: clr, load, up, carry
  assign bit_extender_1_out = {{4{1'b0}}, counter_content};  // Bit_Extender bit_extender_1
  assign controlled_buffer_1_out = Control_Unit_c0 ? counter_content : 4'bz;  // Controlled_Buffer controlled_buffer_1
  reg8bits reg8bits_1 (
    .WE(Control_Unit_c7), .DIN(alu_1_au_dout), .CLOCK(clock_1_out), .OE(Control_Unit_c8), .Reset(in_5),
    .DOUT(reg8bits_1_dout), .stored_data(IR_Content));
  _7_Segment_Display u_7_segment_display_5 (
    .g(decimal_decoder_2_dout[3]), .f(decimal_decoder_2_dout[2]), .a(decimal_decoder_2_dout[1]),
    .b(decimal_decoder_2_dout[0]), .e(decimal_decoder_2_dout[19]), .d(decimal_decoder_2_dout[18]),
    .c(decimal_decoder_2_dout[17]), .dp(decimal_decoder_2_dout[16]));
  Decimal_Decoder decimal_decoder_2 (.Din(bit_extender_1_out), .Dout(decimal_decoder_2_dout));
  Decimal_Decoder decimal_decoder_3 (.Din(Reg_B_Content), .Dout(decimal_decoder_3_dout));
  BitSelector #(.group(4)) bitselector_1 (.in(reg8bits_1_dout), .out(controlled_buffer_1_out), .sel(1'b0));
  reg8bits reg8bits_2 (
    .WE(Control_Unit_c12), .DIN(alu_1_au_dout), .CLOCK(clock_1_out), .Reset(in_6), .stored_data(out_15));  // open: OE, DOUT
  ALU alu_1 (
    .control(Ctrl), .A(out_15), .B(Reg_B_Content), .AU_Sel(AU_Selectors), .LU_Sel(LU_Selectors),
    .OE(Control_Unit_c11), .cout(out_16), .AU_Dout(alu_1_au_dout), .AU_result(AU_Result),
    .LU_result(LU_Result));
  reg8bits reg8bits_3 (
    .WE(Control_Unit_c13), .DIN(alu_1_au_dout), .CLOCK(clock_1_out), .Reset(in_10),
    .stored_data(Reg_B_Content));  // open: OE, DOUT
  _7_Segment_Display u_7_segment_display_6 (
    .g(decimal_decoder_3_dout[15]), .f(decimal_decoder_3_dout[14]), .a(decimal_decoder_3_dout[13]),
    .b(decimal_decoder_3_dout[12]), .e(decimal_decoder_3_dout[31]), .d(decimal_decoder_3_dout[30]),
    .c(decimal_decoder_3_dout[29]), .dp(decimal_decoder_3_dout[28]));
  _7_Segment_Display u_7_segment_display_7 (
    .g(decimal_decoder_3_dout[11]), .f(decimal_decoder_3_dout[10]), .a(decimal_decoder_3_dout[9]),
    .b(decimal_decoder_3_dout[8]), .e(decimal_decoder_3_dout[27]), .d(decimal_decoder_3_dout[26]),
    .c(decimal_decoder_3_dout[25]), .dp(decimal_decoder_3_dout[24]));
  LED led_1 (.in(alu_1_au_dout[7]));
  LED led_2 (.in(alu_1_au_dout[6]));
  _7_Segment_Display u_7_segment_display_8 (
    .g(decimal_decoder_3_dout[7]), .f(decimal_decoder_3_dout[6]), .a(decimal_decoder_3_dout[5]),
    .b(decimal_decoder_3_dout[4]), .e(decimal_decoder_3_dout[23]), .d(decimal_decoder_3_dout[22]),
    .c(decimal_decoder_3_dout[21]), .dp(decimal_decoder_3_dout[20]));
  _7_Segment_Display u_7_segment_display_9 (
    .g(decimal_decoder_3_dout[3]), .f(decimal_decoder_3_dout[2]), .a(decimal_decoder_3_dout[1]),
    .b(decimal_decoder_3_dout[0]), .e(decimal_decoder_3_dout[19]), .d(decimal_decoder_3_dout[18]),
    .c(decimal_decoder_3_dout[17]), .dp(decimal_decoder_3_dout[16]));
  assign alu_1_au_dout = OE ? Test_data : 8'bz;  // Controlled_Buffer controlled_buffer_2
  LED led_3 (.in(alu_1_au_dout[5]));
  LED led_4 (.in(alu_1_au_dout[4]));
  LED led_5 (.in(alu_1_au_dout[3]));
  LED led_6 (.in(alu_1_au_dout[2]));
  LED led_7 (.in(alu_1_au_dout[1]));
  LED led_8 (.in(alu_1_au_dout[0]));
  assign alu_1_au_dout = Control_Unit_c5 ? MBR_Content : 8'bz;  // Controlled_Buffer controlled_buffer_3
  reg8bits Output_Register (
    .WE(Control_Unit_c15), .DIN(alu_1_au_dout), .CLOCK(clock_1_out), .OE(Control_Unit_c14),
    .DOUT(alu_1_au_dout), .stored_data(out_17));  // open: Reset
  reg4bits reg4bits_1 (
    .WE(Control_Unit_c9), .DIN(controlled_buffer_1_out), .CLOCK(clock_1_out), .OE(Control_Unit_c10),
    .DOUT(reg4bits_1_dout), .stored_data(MAR_Content));  // open: Reset
  reg8bits MBR (
    .WE(Control_Unit_c4), .DIN(alu_1_au_dout), .CLOCK(clock_1_out), .OE(Control_Unit_c6),
    .DOUT(alu_1_au_dout), .stored_data(MBR_Content));  // open: Reset
  Decimal_Decoder decimal_decoder_4 (.Din(out_17), .Dout(decimal_decoder_4_dout));
  LED led_9 (.in(alu_1_au_dout[7]));
  LED led_10 (.in(alu_1_au_dout[6]));
  LED led_11 (.in(alu_1_au_dout[5]));
  _7_Segment_Display u_7_segment_display_10 (
    .g(decimal_decoder_4_dout[15]), .f(decimal_decoder_4_dout[14]), .a(decimal_decoder_4_dout[13]),
    .b(decimal_decoder_4_dout[12]), .e(decimal_decoder_4_dout[31]), .d(decimal_decoder_4_dout[30]),
    .c(decimal_decoder_4_dout[29]), .dp(decimal_decoder_4_dout[28]));
  LED led_12 (.in(alu_1_au_dout[4]));
  _7_Segment_Display u_7_segment_display_11 (
    .g(decimal_decoder_4_dout[11]), .f(decimal_decoder_4_dout[10]), .a(decimal_decoder_4_dout[9]),
    .b(decimal_decoder_4_dout[8]), .e(decimal_decoder_4_dout[27]), .d(decimal_decoder_4_dout[26]),
    .c(decimal_decoder_4_dout[25]), .dp(decimal_decoder_4_dout[24]));
  _7_Segment_Display u_7_segment_display_12 (
    .g(decimal_decoder_4_dout[7]), .f(decimal_decoder_4_dout[6]), .a(decimal_decoder_4_dout[5]),
    .b(decimal_decoder_4_dout[4]), .e(decimal_decoder_4_dout[23]), .d(decimal_decoder_4_dout[22]),
    .c(decimal_decoder_4_dout[21]), .dp(decimal_decoder_4_dout[20]));
  assign reg4bits_1_dout = in_1 ? oe_test : 4'bz;  // Controlled_Buffer controlled_buffer_4
  _7_Segment_Display u_7_segment_display_13 (
    .g(decimal_decoder_4_dout[3]), .f(decimal_decoder_4_dout[2]), .a(decimal_decoder_4_dout[1]),
    .b(decimal_decoder_4_dout[0]), .e(decimal_decoder_4_dout[19]), .d(decimal_decoder_4_dout[18]),
    .c(decimal_decoder_4_dout[17]), .dp(decimal_decoder_4_dout[16]));
  LED led_13 (.in(alu_1_au_dout[3]));
  LED led_14 (.in(alu_1_au_dout[2]));
  LED led_15 (.in(alu_1_au_dout[1]));
  LED led_16 (.in(alu_1_au_dout[0]));
  RAM #(.addrWidth(4), .enables("line")) ram_1 (
    .addr(reg4bits_1_dout), .we(Control_Unit_c2), .clk(clock_1_out), .din(alu_1_au_dout), .dout(ram_1_dout));
  BitSelector #(.group(4)) bitselector_2 (.in(IR_Content), .out(bitselector_2_out), .sel(1'b1));
  Counter #(.max('h5), .width(3)) Step_Counter (
    .clk(clock_1_out), .D(undriven), .Q(sc_content));  // open: clr, load, up, count, carry
  assign alu_1_au_dout = Control_Unit_c3 ? ram_1_dout : 8'bz;  // Controlled_Buffer controlled_buffer_5
  Decimal_Decoder decimal_decoder_5 (.Din(bit_extender_2_out), .Dout(out_22));
  assign bit_extender_2_out = {{5{1'b0}}, sc_content};  // Bit_Extender bit_extender_2
  _7_Segment_Display u_7_segment_display_14 (
    .g(out_22[3]), .f(out_22[2]), .a(out_22[1]), .b(out_22[0]), .e(out_22[19]), .d(out_22[18]),
    .c(out_22[17]), .dp(out_22[16]));
  CU Control_Unit (
    .OPC3(bitselector_2_out[3]), .OPC2(bitselector_2_out[2]), .OPC1(bitselector_2_out[1]),
    .OPC0(bitselector_2_out[0]), .SC2(sc_content[2]), .SC1(sc_content[1]), .SC0(sc_content[0]),
    .C0(Control_Unit_c0), .C1(Control_Unit_c1), .C2(Control_Unit_c2), .C3(Control_Unit_c3),
    .C4(Control_Unit_c4), .C5(Control_Unit_c5), .C6(Control_Unit_c6), .C7(Control_Unit_c7),
    .C8(Control_Unit_c8), .C9(Control_Unit_c9), .C10(Control_Unit_c10), .C11(Control_Unit_c11),
    .C12(Control_Unit_c12), .C13(Control_Unit_c13), .C14(Control_Unit_c14), .C15(Control_Unit_c15));

  // Notes on the sheet:
  //   IR Reset
  //   Clock
  //   Reg A Reset
  //   Reg B Reset
  //   Instruction Register
  //   Register A
  //   Register B
  //   Reg A Content
  //   Internal Address Bus
  //   Internal Data Bus
  //   MAR
  //   Intern OE
  //   Output Reg Content
  //   External Address Bus
  //   External Data Bus
endmodule

module Decimal_Decoder (
  input  [7:0] Din,
  output [31:0] Dout
);

  ROM #(.dataWidth(32)) rom_1 (
    .addr(Din),
    .data({Dout[31:28], Dout[15:12], Dout[27:24], Dout[11:8], Dout[23:20], Dout[7:4], Dout[19:16], Dout[3:0]}));

  // Notes on the sheet:
  //   contents of rom_1 (hex, n*v repeats v):
  //   e7 21 cb 6b 2d 6e ee 23 ef 2f 21e7 2121 21cb 216b 212d 216e 21ee 2123 21ef 212f cbe7 cb21 cbcb cb6b
  //   cb2d cb6e cbee cb23 cbef cb2f 6be7 6b21 6bcb 6b6b 6b2d 6b6e 6bee 6b23 6bef 6b2f 2de7 2d21 2dcb 2d6b
  //   2d2d 2d6e 2dee 2d23 2def 2d2f 6ee7 6e21 6ecb 6e6b 6e2d 6e6e 6eee 6e23 6eef 6e2f eee7 ee21 eecb ee6b
  //   ee2d ee6e eeee ee23 eeef ee2f 23e7 2321 23cb 236b 232d 236e 23ee 2323 23ef 232f efe7 ef21 efcb ef6b
  //   ef2d ef6e efee ef23 efef ef2f 2fe7 2f21 2fcb 2f6b 2f2d 2f6e 2fee 2f23 2fef 2f2f 21e7e7 21e721 21e7cb
  //   21e76b 21e72d 21e76e 21e7ee 21e723 21e7ef 21e72f 2121e7 212121 2121cb 21216b 21212d 21216e 2121ee
  //   212123 2121ef 21212f 21cbe7 21cb21 21cbcb 21cb6b 21cb2d 21cb6e 21cbee 21cb23 21cbef 21cb2f 216be7
  //   216b21 216bcb 216b6b 216b2d 216b6e 216bee 216b23 216bef 216b2f 212de7 212d21 212dcb 212d6b 212d2d
  //   212d6e 212dee 212d23 212def 212d2f 216ee7 216e21 216ecb 216e6b 216e2d 216e6e 216eee 216e23 216eef
  //   216e2f 21eee7 21ee21 21eecb 21ee6b 21ee2d 21ee6e 21eeee 21ee23 21eeef 21ee2f 2123e7 212321 2123cb
  //   21236b 21232d 21236e 2123ee 212323 2123ef 21232f 21efe7 21ef21 21efcb 21ef6b 21ef2d 21ef6e 21efee
  //   21ef23 21efef 21ef2f 212fe7 212f21 212fcb 212f6b 212f2d 212f6e 212fee 212f23 212fef 212f2f cbe7e7
  //   cbe721 cbe7cb cbe76b cbe72d cbe76e cbe7ee cbe723 cbe7ef cbe72f cb21e7 cb2121 cb21cb cb216b cb212d
  //   cb216e cb21ee cb2123 cb21ef cb212f cbcbe7 cbcb21 cbcbcb cbcb6b cbcb2d cbcb6e cbcbee cbcb23 cbcbef
  //   cbcb2f cb6be7 cb6b21 cb6bcb cb6b6b cb6b2d cb6b6e cb6bee cb6b23 cb6bef cb6b2f cb2de7 cb2d21 cb2dcb
  //   cb2d6b cb2d2d cb2d6e cb2dee cb2d23 cb2def cb2d2f cb6ee7 cb6e21 cb6ecb cb6e6b cb6e2d cb6e6e
  //   Decimal Decoder
endmodule

module CU (
  input  OPC3,
  input  OPC2,
  input  OPC1,
  input  OPC0,
  input  SC2,
  input  SC1,
  input  SC0,
  output C0,
  output C1,
  output C2,
  output C3,
  output C4,
  output C5,
  output C6,
  output C7,
  output C8,
  output C9,
  output C10,
  output C11,
  output C12,
  output C13,
  output C14,
  output C15
);

  wire and_4_out, and_5_out, and_6_out, and_7_out, and_8_out, and_9_out, and_10_out, and_13_out, and_14_out,
       and_15_out, and_16_out, and_17_out, and_18_out, and_19_out, and_20_out, not_1_out, not_2_out,
       not_3_out, not_4_out, not_5_out;

  not not_1 (not_1_out, OPC1);
  not not_2 (not_2_out, OPC0);
  not not_3 (not_3_out, SC2);
  not not_4 (not_4_out, SC1);
  not not_5 (not_5_out, SC0);
  and and_1 (C0, not_3_out, not_4_out, not_5_out);
  and and_2 (C1, not_3_out, not_4_out, SC0);
  and and_3 (C2, OPC1, OPC0, SC2, not_4_out, not_5_out);
  and and_4 (and_4_out, not_3_out, not_4_out, SC0);
  and and_5 (and_5_out, not_1_out, SC2, not_4_out, not_5_out);
  and and_6 (and_6_out, not_3_out, not_4_out, SC0);
  and and_7 (and_7_out, not_1_out, SC2, not_4_out, not_5_out);
  and and_8 (and_8_out, OPC1, OPC0, not_3_out, SC0);
  and and_9 (and_9_out, not_3_out, SC1, not_5_out);
  and and_10 (and_10_out, not_1_out, SC2, not_4_out, SC0);
  and and_11 (C6, OPC1, OPC0, SC2, not_4_out, not_5_out);
  and and_12 (C7, not_3_out, SC1, not_5_out);
  and and_13 (and_13_out, not_1_out, not_3_out, SC1, SC0);
  and and_14 (and_14_out, OPC0, not_3_out, SC1, SC0);
  and and_15 (and_15_out, not_3_out, not_4_out, not_5_out);
  and and_16 (and_16_out, not_1_out, not_3_out, SC1, SC0);
  and and_17 (and_17_out, OPC0, not_3_out, SC1, SC0);
  and and_18 (and_18_out, not_3_out, not_4_out, SC0);
  and and_19 (and_19_out, not_1_out, SC2, not_4_out, not_5_out);
  and and_20 (and_20_out, OPC0, SC2, not_4_out, not_5_out);
  and and_21 (C11, OPC1, not_2_out, not_3_out, SC1, SC0);
  and and_22 (C12, not_1_out, not_2_out, SC2, not_4_out, SC0);
  and and_23 (C13, not_1_out, OPC0, SC2, not_4_out, SC0);
  and and_24 (C14, OPC1, OPC0, not_3_out, SC1, SC0);
  and and_25 (C15, OPC1, not_2_out, not_3_out, SC1, SC0);
  or or_1 (C3, and_4_out, and_5_out);
  or or_2 (C4, and_6_out, and_7_out, and_8_out);
  or or_3 (C5, and_9_out, and_10_out);
  or or_4 (C8, and_13_out, and_14_out);
  or or_5 (C9, and_15_out, and_16_out, and_17_out);
  or or_6 (C10, and_18_out, and_19_out, and_20_out);
endmodule

module register_file (
  input  [4:0] RA,
  input  [4:0] RB,
  input  [4:0] RW,
  input  RegWrite,
  input  Clock,
  input  [31:0] BusW,
  output [31:0] BusA,
  output [31:0] BusB
);

  wire and_1_out, and_2_out, and_3_out, and_4_out, and_5_out, and_6_out, and_7_out, and_8_out, and_9_out,
       and_10_out, and_11_out, and_12_out, and_13_out, and_14_out, and_15_out, and_16_out, and_17_out,
       and_18_out, and_19_out, and_20_out, and_21_out, and_22_out, and_23_out, and_24_out, and_25_out,
       and_26_out, and_27_out, and_28_out, and_29_out, and_30_out, and_31_out, decoder_1_out1,
       decoder_1_out2, decoder_1_out3, decoder_1_out4, decoder_1_out5, decoder_1_out6, decoder_1_out7,
       decoder_1_out8, decoder_1_out9, decoder_1_out10, decoder_1_out11, decoder_1_out12, decoder_1_out13,
       decoder_1_out14, decoder_1_out15, decoder_1_out16, decoder_1_out17, decoder_1_out18, decoder_1_out19,
       decoder_1_out20, decoder_1_out21, decoder_1_out22, decoder_1_out23, decoder_1_out24, decoder_1_out25,
       decoder_1_out26, decoder_1_out27, decoder_1_out28, decoder_1_out29, decoder_1_out30, decoder_1_out31,
       decoder_2_out0, decoder_2_out1, decoder_2_out2, decoder_2_out3, decoder_2_out4, decoder_2_out5,
       decoder_2_out6, decoder_2_out7, decoder_2_out8, decoder_2_out9, decoder_2_out10, decoder_2_out11,
       decoder_2_out12, decoder_2_out13, decoder_2_out14, decoder_2_out15, decoder_2_out16, decoder_2_out17,
       decoder_2_out18, decoder_2_out19, decoder_2_out20, decoder_2_out21, decoder_2_out22, decoder_2_out23,
       decoder_2_out24, decoder_2_out25, decoder_2_out26, decoder_2_out27, decoder_2_out28, decoder_2_out29,
       decoder_2_out30, decoder_2_out31, decoder_3_out0, decoder_3_out1, decoder_3_out2, decoder_3_out3,
       decoder_3_out4, decoder_3_out5, decoder_3_out6, decoder_3_out7, decoder_3_out8, decoder_3_out9,
       decoder_3_out10, decoder_3_out11, decoder_3_out12, decoder_3_out13, decoder_3_out14, decoder_3_out15,
       decoder_3_out16, decoder_3_out17, decoder_3_out18, decoder_3_out19, decoder_3_out20, decoder_3_out21,
       decoder_3_out22, decoder_3_out23, decoder_3_out24, decoder_3_out25, decoder_3_out26, decoder_3_out27,
       decoder_3_out28, decoder_3_out29, decoder_3_out30, decoder_3_out31;
  wire [31:0] register_1_q, register_2_q, register_3_q, register_4_q, register_5_q, register_6_q,
       register_7_q, register_8_q, register_9_q, register_10_q, register_11_q, register_12_q, register_13_q,
       register_14_q, register_15_q, register_16_q, register_17_q, register_18_q, register_19_q,
       register_20_q, register_21_q, register_22_q, register_23_q, register_24_q, register_25_q,
       register_26_q, register_27_q, register_28_q, register_29_q, register_30_q, register_31_q;

  Decoder #(.enable("false"), .select(5)) decoder_1 (
    .out1(decoder_1_out1), .out2(decoder_1_out2), .out3(decoder_1_out3), .out4(decoder_1_out4),
    .out5(decoder_1_out5), .out6(decoder_1_out6), .out7(decoder_1_out7), .out8(decoder_1_out8),
    .out9(decoder_1_out9), .out10(decoder_1_out10), .out11(decoder_1_out11), .out12(decoder_1_out12),
    .out13(decoder_1_out13), .out14(decoder_1_out14), .out15(decoder_1_out15), .out16(decoder_1_out16),
    .out17(decoder_1_out17), .out18(decoder_1_out18), .out19(decoder_1_out19), .out20(decoder_1_out20),
    .out21(decoder_1_out21), .out22(decoder_1_out22), .out23(decoder_1_out23), .out24(decoder_1_out24),
    .out25(decoder_1_out25), .out26(decoder_1_out26), .out27(decoder_1_out27), .out28(decoder_1_out28),
    .out29(decoder_1_out29), .out30(decoder_1_out30), .out31(decoder_1_out31), .sel(RW));  // open: out0
  and and_1 (and_1_out, decoder_1_out1, RegWrite);
  and and_2 (and_2_out, decoder_1_out2, RegWrite);
  and and_3 (and_3_out, decoder_1_out3, RegWrite);
  and and_4 (and_4_out, decoder_1_out4, RegWrite);
  and and_5 (and_5_out, decoder_1_out5, RegWrite);
  and and_6 (and_6_out, decoder_1_out6, RegWrite);
  and and_7 (and_7_out, decoder_1_out7, RegWrite);
  and and_8 (and_8_out, decoder_1_out8, RegWrite);
  and and_9 (and_9_out, decoder_1_out9, RegWrite);
  and and_10 (and_10_out, decoder_1_out10, RegWrite);
  and and_11 (and_11_out, decoder_1_out11, RegWrite);
  and and_12 (and_12_out, decoder_1_out12, RegWrite);
  and and_13 (and_13_out, decoder_1_out13, RegWrite);
  and and_14 (and_14_out, decoder_1_out14, RegWrite);
  and and_15 (and_15_out, decoder_1_out15, RegWrite);
  and and_16 (and_16_out, decoder_1_out16, RegWrite);
  and and_17 (and_17_out, decoder_1_out17, RegWrite);
  and and_18 (and_18_out, decoder_1_out18, RegWrite);
  and and_19 (and_19_out, decoder_1_out19, RegWrite);
  and and_20 (and_20_out, decoder_1_out20, RegWrite);
  and and_21 (and_21_out, decoder_1_out21, RegWrite);
  and and_22 (and_22_out, decoder_1_out22, RegWrite);
  and and_23 (and_23_out, decoder_1_out23, RegWrite);
  and and_24 (and_24_out, decoder_1_out24, RegWrite);
  and and_25 (and_25_out, decoder_1_out25, RegWrite);
  and and_26 (and_26_out, decoder_1_out26, RegWrite);
  and and_27 (and_27_out, decoder_1_out27, RegWrite);
  and and_28 (and_28_out, decoder_1_out28, RegWrite);
  and and_29 (and_29_out, decoder_1_out29, RegWrite);
  and and_30 (and_30_out, decoder_1_out30, RegWrite);
  and and_31 (and_31_out, decoder_1_out31, RegWrite);
  Register #(.width(32)) register_1 (.D(BusW), .en(and_1_out), .clk(Clock), .Q(register_1_q));  // open: clr
  Register #(.width(32)) register_2 (.D(BusW), .en(and_2_out), .clk(Clock), .Q(register_2_q));  // open: clr
  Register #(.width(32)) register_3 (.D(BusW), .en(and_3_out), .clk(Clock), .Q(register_3_q));  // open: clr
  Register #(.width(32)) register_4 (.D(BusW), .en(and_4_out), .clk(Clock), .Q(register_4_q));  // open: clr
  Register #(.width(32)) register_5 (.D(BusW), .en(and_5_out), .clk(Clock), .Q(register_5_q));  // open: clr
  Register #(.width(32)) register_6 (.D(BusW), .en(and_6_out), .clk(Clock), .Q(register_6_q));  // open: clr
  Register #(.width(32)) register_7 (.D(BusW), .en(and_7_out), .clk(Clock), .Q(register_7_q));  // open: clr
  Register #(.width(32)) register_8 (.D(BusW), .en(and_8_out), .clk(Clock), .Q(register_8_q));  // open: clr
  Register #(.width(32)) register_9 (.D(BusW), .en(and_9_out), .clk(Clock), .Q(register_9_q));  // open: clr
  Register #(.width(32)) register_10 (.D(BusW), .en(and_10_out), .clk(Clock), .Q(register_10_q));  // open: clr
  Register #(.width(32)) register_11 (.D(BusW), .en(and_11_out), .clk(Clock), .Q(register_11_q));  // open: clr
  Register #(.width(32)) register_12 (.D(BusW), .en(and_12_out), .clk(Clock), .Q(register_12_q));  // open: clr
  Register #(.width(32)) register_13 (.D(BusW), .en(and_13_out), .clk(Clock), .Q(register_13_q));  // open: clr
  Register #(.width(32)) register_14 (.D(BusW), .en(and_14_out), .clk(Clock), .Q(register_14_q));  // open: clr
  Register #(.width(32)) register_15 (.D(BusW), .en(and_15_out), .clk(Clock), .Q(register_15_q));  // open: clr
  Register #(.width(32)) register_16 (.D(BusW), .en(and_16_out), .clk(Clock), .Q(register_16_q));  // open: clr
  Register #(.width(32)) register_17 (.D(BusW), .en(and_17_out), .clk(Clock), .Q(register_17_q));  // open: clr
  Register #(.width(32)) register_18 (.D(BusW), .en(and_18_out), .clk(Clock), .Q(register_18_q));  // open: clr
  Register #(.width(32)) register_19 (.D(BusW), .en(and_19_out), .clk(Clock), .Q(register_19_q));  // open: clr
  Register #(.width(32)) register_20 (.D(BusW), .en(and_20_out), .clk(Clock), .Q(register_20_q));  // open: clr
  Register #(.width(32)) register_21 (.D(BusW), .en(and_21_out), .clk(Clock), .Q(register_21_q));  // open: clr
  Register #(.width(32)) register_22 (.D(BusW), .en(and_22_out), .clk(Clock), .Q(register_22_q));  // open: clr
  Register #(.width(32)) register_23 (.D(BusW), .en(and_23_out), .clk(Clock), .Q(register_23_q));  // open: clr
  Register #(.width(32)) register_24 (.D(BusW), .en(and_24_out), .clk(Clock), .Q(register_24_q));  // open: clr
  Register #(.width(32)) register_25 (.D(BusW), .en(and_25_out), .clk(Clock), .Q(register_25_q));  // open: clr
  Register #(.width(32)) register_26 (.D(BusW), .en(and_26_out), .clk(Clock), .Q(register_26_q));  // open: clr
  Register #(.width(32)) register_27 (.D(BusW), .en(and_27_out), .clk(Clock), .Q(register_27_q));  // open: clr
  Register #(.width(32)) register_28 (.D(BusW), .en(and_28_out), .clk(Clock), .Q(register_28_q));  // open: clr
  Register #(.width(32)) register_29 (.D(BusW), .en(and_29_out), .clk(Clock), .Q(register_29_q));  // open: clr
  Register #(.width(32)) register_30 (.D(BusW), .en(and_30_out), .clk(Clock), .Q(register_30_q));  // open: clr
  Register #(.width(32)) register_31 (.D(BusW), .en(and_31_out), .clk(Clock), .Q(register_31_q));  // open: clr
  Decoder #(.enable("false"), .select(5)) decoder_2 (
    .out0(decoder_2_out0), .out1(decoder_2_out1), .out2(decoder_2_out2), .out3(decoder_2_out3),
    .out4(decoder_2_out4), .out5(decoder_2_out5), .out6(decoder_2_out6), .out7(decoder_2_out7),
    .out8(decoder_2_out8), .out9(decoder_2_out9), .out10(decoder_2_out10), .out11(decoder_2_out11),
    .out12(decoder_2_out12), .out13(decoder_2_out13), .out14(decoder_2_out14), .out15(decoder_2_out15),
    .out16(decoder_2_out16), .out17(decoder_2_out17), .out18(decoder_2_out18), .out19(decoder_2_out19),
    .out20(decoder_2_out20), .out21(decoder_2_out21), .out22(decoder_2_out22), .out23(decoder_2_out23),
    .out24(decoder_2_out24), .out25(decoder_2_out25), .out26(decoder_2_out26), .out27(decoder_2_out27),
    .out28(decoder_2_out28), .out29(decoder_2_out29), .out30(decoder_2_out30), .out31(decoder_2_out31),
    .sel(RA));
  assign BusA = decoder_2_out1 ? register_1_q : 32'bz;  // Controlled_Buffer controlled_buffer_1
  assign BusA = decoder_2_out2 ? register_2_q : 32'bz;  // Controlled_Buffer controlled_buffer_2
  assign BusA = decoder_2_out3 ? register_3_q : 32'bz;  // Controlled_Buffer controlled_buffer_3
  assign BusA = decoder_2_out4 ? register_4_q : 32'bz;  // Controlled_Buffer controlled_buffer_4
  assign BusA = decoder_2_out5 ? register_5_q : 32'bz;  // Controlled_Buffer controlled_buffer_5
  assign BusA = decoder_2_out6 ? register_6_q : 32'bz;  // Controlled_Buffer controlled_buffer_6
  assign BusA = decoder_2_out7 ? register_7_q : 32'bz;  // Controlled_Buffer controlled_buffer_7
  assign BusA = decoder_2_out8 ? register_8_q : 32'bz;  // Controlled_Buffer controlled_buffer_8
  assign BusA = decoder_2_out9 ? register_9_q : 32'bz;  // Controlled_Buffer controlled_buffer_9
  assign BusA = decoder_2_out10 ? register_10_q : 32'bz;  // Controlled_Buffer controlled_buffer_10
  assign BusA = decoder_2_out11 ? register_11_q : 32'bz;  // Controlled_Buffer controlled_buffer_11
  assign BusA = decoder_2_out12 ? register_12_q : 32'bz;  // Controlled_Buffer controlled_buffer_12
  assign BusA = decoder_2_out13 ? register_13_q : 32'bz;  // Controlled_Buffer controlled_buffer_13
  assign BusA = decoder_2_out14 ? register_14_q : 32'bz;  // Controlled_Buffer controlled_buffer_14
  assign BusA = decoder_2_out15 ? register_15_q : 32'bz;  // Controlled_Buffer controlled_buffer_15
  assign BusA = decoder_2_out16 ? register_16_q : 32'bz;  // Controlled_Buffer controlled_buffer_16
  assign BusA = decoder_2_out17 ? register_17_q : 32'bz;  // Controlled_Buffer controlled_buffer_17
  assign BusA = decoder_2_out18 ? register_18_q : 32'bz;  // Controlled_Buffer controlled_buffer_18
  assign BusA = decoder_2_out19 ? register_19_q : 32'bz;  // Controlled_Buffer controlled_buffer_19
  assign BusA = decoder_2_out20 ? register_20_q : 32'bz;  // Controlled_Buffer controlled_buffer_20
  assign BusA = decoder_2_out21 ? register_21_q : 32'bz;  // Controlled_Buffer controlled_buffer_21
  assign BusA = decoder_2_out22 ? register_22_q : 32'bz;  // Controlled_Buffer controlled_buffer_22
  assign BusA = decoder_2_out23 ? register_23_q : 32'bz;  // Controlled_Buffer controlled_buffer_23
  assign BusA = decoder_2_out24 ? register_24_q : 32'bz;  // Controlled_Buffer controlled_buffer_24
  assign BusA = decoder_2_out25 ? register_25_q : 32'bz;  // Controlled_Buffer controlled_buffer_25
  assign BusA = decoder_2_out26 ? register_26_q : 32'bz;  // Controlled_Buffer controlled_buffer_26
  assign BusA = decoder_2_out27 ? register_27_q : 32'bz;  // Controlled_Buffer controlled_buffer_27
  assign BusA = decoder_2_out28 ? register_28_q : 32'bz;  // Controlled_Buffer controlled_buffer_28
  assign BusA = decoder_2_out29 ? register_29_q : 32'bz;  // Controlled_Buffer controlled_buffer_29
  assign BusA = decoder_2_out30 ? register_30_q : 32'bz;  // Controlled_Buffer controlled_buffer_30
  assign BusA = decoder_2_out31 ? register_31_q : 32'bz;  // Controlled_Buffer controlled_buffer_31
  Decoder #(.enable("false"), .select(5)) decoder_3 (
    .out0(decoder_3_out0), .out1(decoder_3_out1), .out2(decoder_3_out2), .out3(decoder_3_out3),
    .out4(decoder_3_out4), .out5(decoder_3_out5), .out6(decoder_3_out6), .out7(decoder_3_out7),
    .out8(decoder_3_out8), .out9(decoder_3_out9), .out10(decoder_3_out10), .out11(decoder_3_out11),
    .out12(decoder_3_out12), .out13(decoder_3_out13), .out14(decoder_3_out14), .out15(decoder_3_out15),
    .out16(decoder_3_out16), .out17(decoder_3_out17), .out18(decoder_3_out18), .out19(decoder_3_out19),
    .out20(decoder_3_out20), .out21(decoder_3_out21), .out22(decoder_3_out22), .out23(decoder_3_out23),
    .out24(decoder_3_out24), .out25(decoder_3_out25), .out26(decoder_3_out26), .out27(decoder_3_out27),
    .out28(decoder_3_out28), .out29(decoder_3_out29), .out30(decoder_3_out30), .out31(decoder_3_out31),
    .sel(RB));
  assign BusA = decoder_2_out0 ? {32{1'b0}} : 32'bz;  // Controlled_Buffer controlled_buffer_32
  assign BusB = decoder_3_out1 ? register_1_q : 32'bz;  // Controlled_Buffer controlled_buffer_33
  assign BusB = decoder_3_out2 ? register_2_q : 32'bz;  // Controlled_Buffer controlled_buffer_34
  assign BusB = decoder_3_out3 ? register_3_q : 32'bz;  // Controlled_Buffer controlled_buffer_35
  assign BusB = decoder_3_out4 ? register_4_q : 32'bz;  // Controlled_Buffer controlled_buffer_36
  assign BusB = decoder_3_out5 ? register_5_q : 32'bz;  // Controlled_Buffer controlled_buffer_37
  assign BusB = decoder_3_out6 ? register_6_q : 32'bz;  // Controlled_Buffer controlled_buffer_38
  assign BusB = decoder_3_out7 ? register_7_q : 32'bz;  // Controlled_Buffer controlled_buffer_39
  assign BusB = decoder_3_out8 ? register_8_q : 32'bz;  // Controlled_Buffer controlled_buffer_40
  assign BusB = decoder_3_out9 ? register_9_q : 32'bz;  // Controlled_Buffer controlled_buffer_41
  assign BusB = decoder_3_out10 ? register_10_q : 32'bz;  // Controlled_Buffer controlled_buffer_42
  assign BusB = decoder_3_out11 ? register_11_q : 32'bz;  // Controlled_Buffer controlled_buffer_43
  assign BusB = decoder_3_out12 ? register_12_q : 32'bz;  // Controlled_Buffer controlled_buffer_44
  assign BusB = decoder_3_out13 ? register_13_q : 32'bz;  // Controlled_Buffer controlled_buffer_45
  assign BusB = decoder_3_out14 ? register_14_q : 32'bz;  // Controlled_Buffer controlled_buffer_46
  assign BusB = decoder_3_out15 ? register_15_q : 32'bz;  // Controlled_Buffer controlled_buffer_47
  assign BusB = decoder_3_out16 ? register_16_q : 32'bz;  // Controlled_Buffer controlled_buffer_48
  assign BusB = decoder_3_out17 ? register_17_q : 32'bz;  // Controlled_Buffer controlled_buffer_49
  assign BusB = decoder_3_out18 ? register_18_q : 32'bz;  // Controlled_Buffer controlled_buffer_50
  assign BusB = decoder_3_out19 ? register_19_q : 32'bz;  // Controlled_Buffer controlled_buffer_51
  assign BusB = decoder_3_out20 ? register_20_q : 32'bz;  // Controlled_Buffer controlled_buffer_52
  assign BusB = decoder_3_out21 ? register_21_q : 32'bz;  // Controlled_Buffer controlled_buffer_53
  assign BusB = decoder_3_out22 ? register_22_q : 32'bz;  // Controlled_Buffer controlled_buffer_54
  assign BusB = decoder_3_out23 ? register_23_q : 32'bz;  // Controlled_Buffer controlled_buffer_55
  assign BusB = decoder_3_out24 ? register_24_q : 32'bz;  // Controlled_Buffer controlled_buffer_56
  assign BusB = decoder_3_out25 ? register_25_q : 32'bz;  // Controlled_Buffer controlled_buffer_57
  assign BusB = decoder_3_out26 ? register_26_q : 32'bz;  // Controlled_Buffer controlled_buffer_58
  assign BusB = decoder_3_out27 ? register_27_q : 32'bz;  // Controlled_Buffer controlled_buffer_59
  assign BusB = decoder_3_out28 ? register_28_q : 32'bz;  // Controlled_Buffer controlled_buffer_60
  assign BusB = decoder_3_out29 ? register_29_q : 32'bz;  // Controlled_Buffer controlled_buffer_61
  assign BusB = decoder_3_out30 ? register_30_q : 32'bz;  // Controlled_Buffer controlled_buffer_62
  assign BusB = decoder_3_out31 ? register_31_q : 32'bz;  // Controlled_Buffer controlled_buffer_63
  assign BusB = decoder_3_out0 ? {32{1'b0}} : 32'bz;  // Controlled_Buffer controlled_buffer_64
endmodule

module ALU_32bits (
  input  [1:0] Shift_Op,
  input  ctrl,
  input  Cin,
  input  [31:0] A,
  input  [31:0] B,
  input  [1:0] ALU_Op,
  input  [1:0] Logical_Op,
  output [31:0] out_8,
  output [31:0] out_9,
  output SLT,
  output [31:0] ALU_Result,
  output Cout,
  output [31:0] zero,
  output overflow,
  output [31:0] out_15
);

  wire bitselector_2_out;
  wire [4:0] bitselector_1_out;
  wire [31:0] addsub32bit_1_sum, and_1_out, bit_extender_1_out, bit_shifter_1_shifted_bits,
       multiplexer_1_out, not_1_out, or_1_out, xor_1_out;

  BitSelector #(.group(5), .width(32)) bitselector_1 (.in(A), .out(bitselector_1_out), .sel(3'b000));
  assign and_1_out = A & B;  // AND_Gate and_1, 32 bits wide
  assign or_1_out = A | B;  // OR_Gate or_1, 32 bits wide
  assign xor_1_out = A ^ B;  // XOR_Gate xor_1, 32 bits wide
  bit_shifter bit_shifter_1 (
    .input_bits(B), .sa(bitselector_1_out), .selector(Shift_Op), .shifted_bits(bit_shifter_1_shifted_bits));
  addsub32bit addsub32bit_1 (
    .ctrl(ctrl), .Cin(Cin), .A(A), .B(B), .sum(addsub32bit_1_sum), .Cout(Cout), .Overflow(overflow));
  assign not_1_out = ~or_1_out;  // NOT_Gate not_1, 32 bits wide
  BitSelector #(.width(32)) bitselector_2 (.in(addsub32bit_1_sum), .out(bitselector_2_out), .sel({5{1'b1}}));
  assign bit_extender_1_out = {{31{SLT}}, SLT};  // Bit_Extender bit_extender_1
  Comparator #(.width(1)) comparator_1 (.a(bitselector_2_out), .b(overflow), .eq(SLT));  // open: gt, lt
  Multiplexer #(.select(2), .width(32)) multiplexer_1 (
    .in0(and_1_out), .in1(or_1_out), .in2(not_1_out), .in3(xor_1_out), .out(multiplexer_1_out),
    .sel(Logical_Op));
  Multiplexer #(.select(2), .width(32)) multiplexer_2 (
    .in0(bit_shifter_1_shifted_bits), .in1(bit_extender_1_out), .in2(addsub32bit_1_sum),
    .in3(multiplexer_1_out), .out(ALU_Result), .sel(ALU_Op));
  assign zero = ~(ALU_Result | ALU_Result);  // NOR_Gate nor_1, 32 bits wide

  assign out_8 = A;
  assign out_9 = ALU_Result;
  assign out_15 = B;
endmodule

module addsub32bit (
  input  ctrl,
  input  Cin,
  input  [31:0] A,
  input  [31:0] B,
  output [31:0] sum,
  output Cout,
  output Overflow
);

  wire addsub8bit_1_carry, addsub8bit_2_carry, addsub8bit_3_carry;

  addsub8bit addsub8bit_1 (
    .control(ctrl), .A(A[7:0]), .cin(Cin), .B(B[7:0]), .sum(sum[7:0]), .carry(addsub8bit_1_carry));  // open: overflow
  addsub8bit addsub8bit_2 (
    .control(ctrl), .A(A[15:8]), .cin(addsub8bit_1_carry), .B(B[15:8]), .sum(sum[15:8]),
    .carry(addsub8bit_2_carry));  // open: overflow
  addsub8bit addsub8bit_3 (
    .control(ctrl), .A(A[23:16]), .cin(addsub8bit_2_carry), .B(B[23:16]), .sum(sum[23:16]),
    .carry(addsub8bit_3_carry));  // open: overflow
  addsub8bit addsub8bit_4 (
    .control(ctrl), .A(A[31:24]), .cin(addsub8bit_3_carry), .B(B[31:24]), .sum(sum[31:24]), .carry(Cout),
    .overflow(Overflow));
endmodule

module bit_shifter (
  input  [31:0] input_bits,
  input  [4:0] sa,
  input  [1:0] selector,
  output [31:0] shifted_bits
);

  wire [31:0] shifter_1_out, shifter_2_out, shifter_3_out;

  Shifter #(.width(32)) shifter_1 (.in(input_bits), .\dist (sa), .out(shifter_1_out));
  Shifter #(.shift("lr"), .width(32)) shifter_2 (.in(input_bits), .\dist (sa), .out(shifter_2_out));
  Shifter #(.shift("ar"), .width(32)) shifter_3 (.in(input_bits), .\dist (sa), .out(shifter_3_out));
  Multiplexer #(.select(2), .width(32)) multiplexer_1 (
    .in1(shifter_1_out), .in2(shifter_2_out), .in3(shifter_3_out), .out(shifted_bits), .sel(selector));  // open: in0
endmodule

module reg16bits (
  input  WE,
  input  [15:0] DIN,
  input  CLOCK,
  input  OE,
  input  Reset,
  output [15:0] DOUT,
  output [7:0] Eight_LSBs,
  output [7:0] Eight_MSBs,
  output [15:0] stored_data
);

  reg8bits reg8bits_1 (
    .WE(WE), .DIN(DIN[7:0]), .CLOCK(CLOCK), .OE(OE), .Reset(Reset), .DOUT(DOUT[7:0]),
    .stored_data(stored_data[7:0]));
  reg8bits reg8bits_2 (
    .WE(WE), .DIN(DIN[15:8]), .CLOCK(CLOCK), .OE(OE), .Reset(Reset), .DOUT(DOUT[15:8]),
    .stored_data(stored_data[15:8]));
  BitSelector #(.group(8), .width(16)) bitselector_1 (.in(DOUT), .out(Eight_LSBs), .sel(1'b0));
  BitSelector #(.group(8), .width(16)) bitselector_2 (.in(DOUT), .out(Eight_MSBs), .sel(1'b1));
endmodule

module Decimal_Decoder16 (
  input  [15:0] Din,
  output [31:0] Dout
);

  ROM #(.addrWidth(16), .dataWidth(32)) rom_1 (
    .addr(Din),
    .data({Dout[31:28], Dout[15:12], Dout[27:24], Dout[11:8], Dout[23:20], Dout[7:4], Dout[19:16], Dout[3:0]}));

  // Notes on the sheet:
  //   contents of rom_1 (hex, n*v repeats v):
  //   e7 21 cb 6b 2d 6e ee 23 ef 2f 21e7 2121 21cb 216b 212d 216e 21ee 2123 21ef 212f cbe7 cb21 cbcb cb6b
  //   cb2d cb6e cbee cb23 cbef cb2f 6be7 6b21 6bcb 6b6b 6b2d 6b6e 6bee 6b23 6bef 6b2f 2de7 2d21 2dcb 2d6b
  //   2d2d 2d6e 2dee 2d23 2def 2d2f 6ee7 6e21 6ecb 6e6b 6e2d 6e6e 6eee 6e23 6eef 6e2f eee7 ee21 eecb ee6b
  //   ee2d ee6e eeee ee23 eeef ee2f 23e7 2321 23cb 236b 232d 236e 23ee 2323 23ef 232f efe7 ef21 efcb ef6b
  //   ef2d ef6e efee ef23 efef ef2f 2fe7 2f21 2fcb 2f6b 2f2d 2f6e 2fee 2f23 2fef 2f2f 21e7e7 21e721 21e7cb
  //   21e76b 21e72d 21e76e 21e7ee 21e723 21e7ef 21e72f 2121e7 212121 2121cb 21216b 21212d 21216e 2121ee
  //   212123 2121ef 21212f 21cbe7 21cb21 21cbcb 21cb6b 21cb2d 21cb6e 21cbee 21cb23 21cbef 21cb2f 216be7
  //   216b21 216bcb 216b6b 216b2d 216b6e 216bee 216b23 216bef 216b2f 212de7 212d21 212dcb 212d6b 212d2d
  //   212d6e 212dee 212d23 212def 212d2f 216ee7 216e21 216ecb 216e6b 216e2d 216e6e 216eee 216e23 216eef
  //   216e2f 21eee7 21ee21 21eecb 21ee6b 21ee2d 21ee6e 21eeee 21ee23 21eeef 21ee2f 2123e7 212321 2123cb
  //   21236b 21232d 21236e 2123ee 212323 2123ef 21232f 21efe7 21ef21 21efcb 21ef6b 21ef2d 21ef6e 21efee
  //   21ef23 21efef 21ef2f 212fe7 212f21 212fcb 212f6b 212f2d 212f6e 212fee 212f23 212fef 212f2f cbe7e7
  //   cbe721 cbe7cb cbe76b cbe72d cbe76e cbe7ee cbe723 cbe7ef cbe72f cb21e7 cb2121 cb21cb cb216b cb212d
  //   cb216e cb21ee cb2123 cb21ef cb212f cbcbe7 cbcb21 cbcbcb cbcb6b cbcb2d cbcb6e cbcbee cbcb23 cbcbef
  //   cbcb2f cb6be7 cb6b21 cb6bcb cb6b6b cb6b2d cb6b6e cb6bee cb6b23 cb6bef cb6b2f cb2de7 cb2d21 cb2dcb
  //   cb2d6b cb2d2d cb2d6e cb2dee cb2d23 cb2def cb2d2f cb6ee7 cb6e21 cb6ecb cb6e6b cb6e2d cb6e6e
  //   Decimal Decoder
endmodule

module project_alu (
  input  [15:0] A,
  input  [15:0] B,
  input  [3:0] AUSel,
  input  [2:0] RUSel,
  input  OE,
  output [15:0] AUResult,
  output RUResult,
  output [15:0] AUDout
);

  project_ao project_ao_1 (.A(A), .B(B), .AUSel(AUSel), .AUResult(AUResult));
  project_ro project_ro_1 (.A(A), .B(B), .RUSel(RUSel), .RUResult(RUResult));
  assign AUDout = OE ? AUResult : 16'bz;  // Controlled_Buffer controlled_buffer_1
endmodule

module project_ao (
  input  [15:0] A,
  input  [15:0] B,
  input  [3:0] AUSel,
  output [15:0] AUResult
);

  wire [15:0] adder_1_out, and_1_out, divider_1_out, divider_1_rem, multiplier_1_out, negator_1_out,
       negator_2_out, or_1_out, shifter_1_out, shifter_2_out, shifter_3_out, shifter_4_out, subtractor_1_out,
       xor_1_out;

  Adder #(.width(16)) adder_1 (.a(A), .b(B), .out(adder_1_out));  // open: cin, cout
  assign and_1_out = A & B;  // AND_Gate and_1, 16 bits wide
  assign or_1_out = A | B;  // OR_Gate or_1, 16 bits wide
  assign xor_1_out = A ^ B;  // XOR_Gate xor_1, 16 bits wide
  Divider #(.width(16)) divider_1 (.a(A), .b(B), .out(divider_1_out), .rem(divider_1_rem));  // open: upper
  Multiplier #(.width(16)) multiplier_1 (.a(A), .b(B), .out(multiplier_1_out));  // open: cin, cout
  Subtractor #(.width(16)) subtractor_1 (.a(A), .b(B), .out(subtractor_1_out));  // open: bin, bout
  Shifter #(.width(16)) shifter_1 (.in(A), .\dist (4'b0010), .out(shifter_1_out));
  Shifter #(.width(16)) shifter_2 (.in(B), .\dist (4'b0010), .out(shifter_2_out));
  Shifter #(.shift("lr"), .width(16)) shifter_3 (.in(A), .\dist (4'b0010), .out(shifter_3_out));
  Shifter #(.shift("lr"), .width(16)) shifter_4 (.in(B), .\dist (4'b0010), .out(shifter_4_out));
  Negator #(.width(16)) negator_1 (.in(A), .out(negator_1_out));
  Negator #(.width(16)) negator_2 (.in(B), .out(negator_2_out));
  Multiplexer #(.select(4), .width(16)) multiplexer_1 (
    .in0(adder_1_out), .in1(and_1_out), .in2(or_1_out), .in3(xor_1_out), .in4(divider_1_out),
    .in5(divider_1_rem), .in6(multiplier_1_out), .in7(subtractor_1_out), .in8(shifter_1_out),
    .in9(shifter_2_out), .in10(shifter_3_out), .in11(shifter_4_out), .in12(negator_1_out),
    .in13(negator_2_out), .out(AUResult), .sel(AUSel));  // open: in14, in15
endmodule

module project_ro (
  input  [15:0] A,
  input  [15:0] B,
  input  [2:0] RUSel,
  output RUResult
);

  wire comparator_1_eq, comparator_1_gt, comparator_1_lt, not_1_out, or_1_out, or_2_out;

  or or_1 (or_1_out, comparator_1_gt, comparator_1_eq);
  Comparator #(.width(16)) comparator_1 (
    .a(A), .b(B), .gt(comparator_1_gt), .eq(comparator_1_eq), .lt(comparator_1_lt));
  or or_2 (or_2_out, comparator_1_lt, comparator_1_eq);
  not not_1 (not_1_out, comparator_1_eq);
  Multiplexer #(.select(3)) multiplexer_1 (
    .in0(comparator_1_gt), .in1(comparator_1_eq), .in2(or_1_out), .in3(comparator_1_lt), .in4(or_2_out),
    .in5(not_1_out), .out(RUResult), .sel(RUSel));  // open: in6, in7
endmodule
