// Logisim project Group1_PartA.circ as structural Verilog: 10 circuits, main circuit main
module main (
  input  [15:0] in_1
);

  wire [31:0] decimal_decoder16_1_dout;

  Decimal_Decoder16 decimal_decoder16_1 (.Din(in_1), .Dout(decimal_decoder16_1_dout));
  _7_Segment_Display u_7_segment_display_1 (
    .g(decimal_decoder16_1_dout[15]), .f(decimal_decoder16_1_dout[14]), .a(decimal_decoder16_1_dout[13]),
    .b(decimal_decoder16_1_dout[12]), .e(decimal_decoder16_1_dout[31]), .d(decimal_decoder16_1_dout[30]),
    .c(decimal_decoder16_1_dout[29]), .dp(decimal_decoder16_1_dout[28]));
  _7_Segment_Display u_7_segment_display_2 (
    .g(decimal_decoder16_1_dout[11]), .f(decimal_decoder16_1_dout[10]), .a(decimal_decoder16_1_dout[9]),
    .b(decimal_decoder16_1_dout[8]), .e(decimal_decoder16_1_dout[27]), .d(decimal_decoder16_1_dout[26]),
    .c(decimal_decoder16_1_dout[25]), .dp(decimal_decoder16_1_dout[24]));
  _7_Segment_Display u_7_segment_display_3 (
    .g(decimal_decoder16_1_dout[7]), .f(decimal_decoder16_1_dout[6]), .a(decimal_decoder16_1_dout[5]),
    .b(decimal_decoder16_1_dout[4]), .e(decimal_decoder16_1_dout[23]), .d(decimal_decoder16_1_dout[22]),
    .c(decimal_decoder16_1_dout[21]), .dp(decimal_decoder16_1_dout[20]));
  _7_Segment_Display u_7_segment_display_4 (
    .g(decimal_decoder16_1_dout[3]), .f(decimal_decoder16_1_dout[2]), .a(decimal_decoder16_1_dout[1]),
    .b(decimal_decoder16_1_dout[0]), .e(decimal_decoder16_1_dout[19]), .d(decimal_decoder16_1_dout[18]),
    .c(decimal_decoder16_1_dout[17]), .dp(decimal_decoder16_1_dout[16]));
endmodule

module project_alu (
  input  [15:0] A,
  input  [15:0] B,
  input  [3:0] AUSel,
  input  [2:0] RUSel,
  input  OE,
  output [15:0] AUResult,
  output RUResult,
  output [15:0] AUDout
);

  project_ao project_ao_1 (.A(A), .B(B), .AUSel(AUSel), .AUResult(AUResult));
  project_ro project_ro_1 (.A(A), .B(B), .RUSel(RUSel), .RUResult(RUResult));
  assign AUDout = OE ? AUResult : 16'bz;  // Controlled_Buffer controlled_buffer_1
endmodule

module project_ao (
  input  [15:0] A,
  input  [15:0] B,
  input  [3:0] AUSel,
  output [15:0] AUResult
);

  wire [15:0] adder_1_out, and_1_out, divider_1_out, divider_1_rem, multiplier_1_out, negator_1_out,
       negator_2_out, or_1_out, shifter_1_out, shifter_2_out, shifter_3_out, shifter_4_out, subtractor_1_out,
       xor_1_out;

  Adder #(.width(16)) adder_1 (.a(A), .b(B), .out(adder_1_out));  // open: cin, cout
  assign and_1_out = A & B;  // AND_Gate and_1, 16 bits wide
  assign or_1_out = A | B;  // OR_Gate or_1, 16 bits wide
  assign xor_1_out = A ^ B;  // XOR_Gate xor_1, 16 bits wide
  Divider #(.width(16)) divider_1 (.a(A), .b(B), .out(divider_1_out), .rem(divider_1_rem));  // open: upper
  Multiplier #(.width(16)) multiplier_1 (.a(A), .b(B), .out(multiplier_1_out));  // open: cin, cout
  Subtractor #(.width(16)) subtractor_1 (.a(A), .b(B), .out(subtractor_1_out));  // open: bin, bout
  Shifter #(.width(16)) shifter_1 (.in(A), .\dist (4'b0010), .out(shifter_1_out));
  Shifter #(.width(16)) shifter_2 (.in(B), .\dist (4'b0010), .out(shifter_2_out));
  Shifter #(.shift("lr"), .width(16)) shifter_3 (.in(A), .\dist (4'b0010), .out(shifter_3_out));
  Shifter #(.shift("lr"), .width(16)) shifter_4 (.in(B), .\dist (4'b0010), .out(shifter_4_out));
  Negator #(.width(16)) negator_1 (.in(A), .out(negator_1_out));
  Negator #(.width(16)) negator_2 (.in(B), .out(negator_2_out));
  Multiplexer #(.select(4), .width(16)) multiplexer_1 (
    .in0(adder_1_out), .in1(and_1_out), .in2(or_1_out), .in3(xor_1_out), .in4(divider_1_out),
    .in5(divider_1_rem), .in6(multiplier_1_out), .in7(subtractor_1_out), .in8(shifter_1_out),
    .in9(shifter_2_out), .in10(shifter_3_out), .in11(shifter_4_out), .in12(negator_1_out),
    .in13(negator_2_out), .out(AUResult), .sel(AUSel));  // open: in14, in15
endmodule

module project_ro (
  input  [15:0] A,
  input  [15:0] B,
  input  [2:0] RUSel,
  output RUResult
);

  wire comparator_1_eq, comparator_1_gt, comparator_1_lt, not_1_out, or_1_out, or_2_out;

  or or_1 (or_1_out, comparator_1_gt, comparator_1_eq);
  Comparator #(.width(16)) comparator_1 (
    .a(A), .b(B), .gt(comparator_1_gt), .eq(comparator_1_eq), .lt(comparator_1_lt));
  or or_2 (or_2_out, comparator_1_lt, comparator_1_eq);
  not not_1 (not_1_out, comparator_1_eq);
  Multiplexer #(.select(3)) multiplexer_1 (
    .in0(comparator_1_gt), .in1(comparator_1_eq), .in2(or_1_out), .in3(comparator_1_lt), .in4(or_2_out),
    .in5(not_1_out), .out(RUResult), .sel(RUSel));  // open: in6, in7
endmodule

module project_register_16 (
  input  [15:0] input_val,
  input  WE,
  input  clk,
  input  reset,
  input  OE,
  output [15:0] result,
  output [15:0] Dout,
  output [7:0] Eight_LSB,
  output [7:0] Eight_MSB
);

  Register #(.width(16)) register_1 (.D(input_val), .en(WE), .clk(clk), .Q(result), .clr(reset));
  assign Dout = OE ? result : 16'bz;  // Controlled_Buffer controlled_buffer_1
  BitSelector #(.group(8), .width(16)) bitselector_1 (.in(result), .out(Eight_MSB), .sel(1'b1));
  BitSelector #(.group(8), .width(16)) bitselector_2 (.in(Dout), .out(Eight_LSB), .sel(1'b0));
endmodule

module project_register_8 (
  input  [7:0] input_val,
  input  WE,
  input  clk,
  input  reset,
  input  OE,
  output [7:0] result,
  output [7:0] Dout,
  output [3:0] Eight_LSB,
  output [3:0] Eight_MSB
);

  Register register_1 (.D(input_val), .en(WE), .clk(clk), .Q(result), .clr(reset));
  assign Dout = OE ? result : 8'bz;  // Controlled_Buffer controlled_buffer_1
  BitSelector #(.group(4)) bitselector_1 (.in(Dout), .out(Eight_LSB), .sel(1'b0));
  BitSelector #(.group(4)) bitselector_2 (.in(Dout), .out(Eight_MSB), .sel(1'b1));
endmodule

module Datapath (
  input  PC_OE,
  input  CE,
  input  MAR_WE,
  input  in_4,
  input  in_5,
  input  MAR_OE,
  input  [7:0] in_7,
  input  WE,
  input  [15:0] in_9,
  input  in_10,
  input  MBR_IOE,
  input  MBR_WE,
  input  in_13,
  input  MBR_OE,
  input  RAM_OE,
  input  IR_WE,
  input  in_17,
  input  IR_OE,
  input  REG_A_WE,
  input  in_20,
  input  REG_A_OE,
  input  OR_WE,
  input  in_23,
  input  OR_OE,
  input  [3:0] AUSel,
  input  [2:0] RUSel,
  input  ALU_OE,
  input  REG_B_WE,
  input  in_29,
  input  in_30,
  output [7:0] out_31,
  output [7:0] out_32,
  output [15:0] out_33,
  output [15:0] out_34,
  output [15:0] out_35,
  output [15:0] out_36,
  output [7:0] out_37,
  output [7:0] out_38,
  output [15:0] out_39,
  output [15:0] out_40,
  output [15:0] out_41,
  output [15:0] out_42,
  output [15:0] out_43
);

  wire clock_1_out, undriven;
  wire [3:0] counter_1_q;
  wire [7:0] MAR_dout;
  wire [15:0] bit_extender_1_out, ram_1_dout;
  wire [31:0] decimal_decoder16_1_dout, decimal_decoder16_2_dout, decimal_decoder16_3_dout,
       decimal_decoder16_4_dout;

  Clock clock_1 (.out(clock_1_out));
  Counter #(.max('h3), .width(4)) counter_1 (
    .count(CE), .clk(clock_1_out), .D(out_31[3:0]), .Q(counter_1_q));  // open: clr, load, up, carry
  assign bit_extender_1_out = {{12{counter_1_q[3]}}, counter_1_q};  // Bit_Extender bit_extender_1
  project_register_16 IR (
    .input_val(out_33), .WE(IR_WE), .clk(clock_1_out), .reset(in_17), .OE(IR_OE), .result(out_35),
    .Eight_LSB(out_31), .Eight_MSB(out_38));  // open: Dout
  project_register_16 RegA (
    .input_val(out_33), .WE(REG_A_WE), .clk(clock_1_out), .reset(in_20), .OE(REG_A_OE), .result(out_40));  // open: Dout, Eight_LSB, Eight_MSB
  project_alu project_alu_1 (
    .A(out_40), .B(out_43), .AUSel(AUSel), .RUSel(RUSel), .OE(ALU_OE), .AUResult(out_42), .AUDout(out_33));  // open: RUResult
  assign out_31[3:0] = PC_OE ? counter_1_q : 4'bz;  // Controlled_Buffer controlled_buffer_1
  project_register_16 RegB (
    .input_val(out_33), .WE(REG_B_WE), .clk(clock_1_out), .reset(in_29), .OE(in_30), .result(out_43));  // open: Dout, Eight_LSB, Eight_MSB
  Decimal_Decoder16 decimal_decoder16_1 (.Din(bit_extender_1_out), .Dout(decimal_decoder16_1_dout));
  _7_Segment_Display u_7_segment_display_1 (
    .g(decimal_decoder16_1_dout[15]), .f(decimal_decoder16_1_dout[14]), .a(decimal_decoder16_1_dout[13]),
    .b(decimal_decoder16_1_dout[12]), .e(decimal_decoder16_1_dout[31]), .d(decimal_decoder16_1_dout[30]),
    .c(decimal_decoder16_1_dout[29]), .dp(decimal_decoder16_1_dout[28]));
  _7_Segment_Display u_7_segment_display_2 (
    .g(decimal_decoder16_1_dout[11]), .f(decimal_decoder16_1_dout[10]), .a(decimal_decoder16_1_dout[9]),
    .b(decimal_decoder16_1_dout[8]), .e(decimal_decoder16_1_dout[27]), .d(decimal_decoder16_1_dout[26]),
    .c(decimal_decoder16_1_dout[25]), .dp(decimal_decoder16_1_dout[24]));
  _7_Segment_Display u_7_segment_display_3 (
    .g(decimal_decoder16_1_dout[7]), .f(decimal_decoder16_1_dout[6]), .a(decimal_decoder16_1_dout[5]),
    .b(decimal_decoder16_1_dout[4]), .e(decimal_decoder16_1_dout[23]), .d(decimal_decoder16_1_dout[22]),
    .c(decimal_decoder16_1_dout[21]), .dp(decimal_decoder16_1_dout[20]));
  _7_Segment_Display u_7_segment_display_4 (
    .g(decimal_decoder16_1_dout[3]), .f(decimal_decoder16_1_dout[2]), .a(decimal_decoder16_1_dout[1]),
    .b(decimal_decoder16_1_dout[0]), .e(decimal_decoder16_1_dout[19]), .d(decimal_decoder16_1_dout[18]),
    .c(decimal_decoder16_1_dout[17]), .dp(decimal_decoder16_1_dout[16]));
  Decimal_Decoder16 decimal_decoder16_2 (.Din(out_43), .Dout(decimal_decoder16_2_dout));
  Decimal_Decoder16 decimal_decoder16_3 (.Din(out_40), .Dout(decimal_decoder16_3_dout));
  _7_Segment_Display u_7_segment_display_5 (
    .g(decimal_decoder16_2_dout[15]), .f(decimal_decoder16_2_dout[14]), .a(decimal_decoder16_2_dout[13]),
    .b(decimal_decoder16_2_dout[12]), .e(decimal_decoder16_2_dout[31]), .d(decimal_decoder16_2_dout[30]),
    .c(decimal_decoder16_2_dout[29]), .dp(decimal_decoder16_2_dout[28]));
  _7_Segment_Display u_7_segment_display_6 (
    .g(decimal_decoder16_3_dout[15]), .f(decimal_decoder16_3_dout[14]), .a(decimal_decoder16_3_dout[13]),
    .b(decimal_decoder16_3_dout[12]), .e(decimal_decoder16_3_dout[31]), .d(decimal_decoder16_3_dout[30]),
    .c(decimal_decoder16_3_dout[29]), .dp(decimal_decoder16_3_dout[28]));
  _7_Segment_Display u_7_segment_display_7 (
    .g(decimal_decoder16_3_dout[11]), .f(decimal_decoder16_3_dout[10]), .a(decimal_decoder16_3_dout[9]),
    .b(decimal_decoder16_3_dout[8]), .e(decimal_decoder16_3_dout[27]), .d(decimal_decoder16_3_dout[26]),
    .c(decimal_decoder16_3_dout[25]), .dp(decimal_decoder16_3_dout[24]));
  _7_Segment_Display u_7_segment_display_8 (
    .g(decimal_decoder16_2_dout[11]), .f(decimal_decoder16_2_dout[10]), .a(decimal_decoder16_2_dout[9]),
    .b(decimal_decoder16_2_dout[8]), .e(decimal_decoder16_2_dout[27]), .d(decimal_decoder16_2_dout[26]),
    .c(decimal_decoder16_2_dout[25]), .dp(decimal_decoder16_2_dout[24]));
  _7_Segment_Display u_7_segment_display_9 (
    .g(decimal_decoder16_2_dout[7]), .f(decimal_decoder16_2_dout[6]), .a(decimal_decoder16_2_dout[5]),
    .b(decimal_decoder16_2_dout[4]), .e(decimal_decoder16_2_dout[23]), .d(decimal_decoder16_2_dout[22]),
    .c(decimal_decoder16_2_dout[21]), .dp(decimal_decoder16_2_dout[20]));
  _7_Segment_Display u_7_segment_display_10 (
    .g(decimal_decoder16_3_dout[7]), .f(decimal_decoder16_3_dout[6]), .a(decimal_decoder16_3_dout[5]),
    .b(decimal_decoder16_3_dout[4]), .e(decimal_decoder16_3_dout[23]), .d(decimal_decoder16_3_dout[22]),
    .c(decimal_decoder16_3_dout[21]), .dp(decimal_decoder16_3_dout[20]));
  _7_Segment_Display u_7_segment_display_11 (
    .g(decimal_decoder16_3_dout[3]), .f(decimal_decoder16_3_dout[2]), .a(decimal_decoder16_3_dout[1]),
    .b(decimal_decoder16_3_dout[0]), .e(decimal_decoder16_3_dout[19]), .d(decimal_decoder16_3_dout[18]),
    .c(decimal_decoder16_3_dout[17]), .dp(decimal_decoder16_3_dout[16]));
  _7_Segment_Display u_7_segment_display_12 (
    .g(decimal_decoder16_2_dout[3]), .f(decimal_decoder16_2_dout[2]), .a(decimal_decoder16_2_dout[1]),
    .b(decimal_decoder16_2_dout[0]), .e(decimal_decoder16_2_dout[19]), .d(decimal_decoder16_2_dout[18]),
    .c(decimal_decoder16_2_dout[17]), .dp(decimal_decoder16_2_dout[16]));
  assign out_33 = in_10 ? in_9 : 16'bz;  // Controlled_Buffer controlled_buffer_2
  assign out_33 = MBR_IOE ? out_34 : 16'bz;  // Controlled_Buffer controlled_buffer_3
  project_register_16 MBR (
    .input_val(out_33), .WE(MBR_WE), .clk(clock_1_out), .reset(in_13), .OE(MBR_OE), .result(out_34),
    .Dout(out_33));  // open: Eight_LSB, Eight_MSB
  project_register_8 MAR (
    .input_val(out_31), .WE(MAR_WE), .clk(clock_1_out), .reset(in_4), .OE(MAR_OE), .result(out_32),
    .Dout(MAR_dout));  // open: Eight_LSB, Eight_MSB
  project_register_16 OutReg (
    .input_val(out_33), .WE(OR_WE), .clk(clock_1_out), .reset(in_23), .OE(OR_OE), .result(out_41),
    .Dout(out_33));  // open: Eight_LSB, Eight_MSB
  Decimal_Decoder16 decimal_decoder16_4 (.Din(out_41), .Dout(decimal_decoder16_4_dout));
  _7_Segment_Display u_7_segment_display_13 (
    .g(decimal_decoder16_4_dout[15]), .f(decimal_decoder16_4_dout[14]), .a(decimal_decoder16_4_dout[13]),
    .b(decimal_decoder16_4_dout[12]), .e(decimal_decoder16_4_dout[31]), .d(decimal_decoder16_4_dout[30]),
    .c(decimal_decoder16_4_dout[29]), .dp(decimal_decoder16_4_dout[28]));
  _7_Segment_Display u_7_segment_display_14 (
    .g(decimal_decoder16_4_dout[11]), .f(decimal_decoder16_4_dout[10]), .a(decimal_decoder16_4_dout[9]),
    .b(decimal_decoder16_4_dout[8]), .e(decimal_decoder16_4_dout[27]), .d(decimal_decoder16_4_dout[26]),
    .c(decimal_decoder16_4_dout[25]), .dp(decimal_decoder16_4_dout[24]));
  _7_Segment_Display u_7_segment_display_15 (
    .g(decimal_decoder16_4_dout[7]), .f(decimal_decoder16_4_dout[6]), .a(decimal_decoder16_4_dout[5]),
    .b(decimal_decoder16_4_dout[4]), .e(decimal_decoder16_4_dout[23]), .d(decimal_decoder16_4_dout[22]),
    .c(decimal_decoder16_4_dout[21]), .dp(decimal_decoder16_4_dout[20]));
  _7_Segment_Display u_7_segment_display_16 (
    .g(decimal_decoder16_4_dout[3]), .f(decimal_decoder16_4_dout[2]), .a(decimal_decoder16_4_dout[1]),
    .b(decimal_decoder16_4_dout[0]), .e(decimal_decoder16_4_dout[19]), .d(decimal_decoder16_4_dout[18]),
    .c(decimal_decoder16_4_dout[17]), .dp(decimal_decoder16_4_dout[16]));
  assign MAR_dout = in_5 ? in_7 : 8'bz;  // Controlled_Buffer controlled_buffer_4
  assign out_33 = RAM_OE ? ram_1_dout : 16'bz;  // Controlled_Buffer controlled_buffer_5
  RAM #(.dataWidth(16), .enables("line")) ram_1 (
    .addr(MAR_dout), .we(WE), .oe(undriven), .clk(clock_1_out), .din(out_33), .dout(ram_1_dout));

  assign out_36 = out_33;
  assign out_37 = out_31;
  assign out_39 = out_33;
endmodule

module CPU (
  input  MAR_OE,
  input  MAR_WE,
  input  CE,
  input  PC_OE,
  input  in_5,
  input  in_6,
  input  [7:0] in_7,
  input  WE,
  input  [15:0] in_9,
  input  in_10,
  input  MBR_IOE,
  input  in_12,
  input  RAM_OE,
  input  in_14,
  input  MBR_OE,
  input  MBR_WE,
  input  in_17,
  input  REG_A_OE,
  input  in_19,
  input  [3:0] AUSel,
  input  [2:0] RUSel,
  input  in_22,
  input  in_23,
  input  IR_WE,
  input  IR_OE,
  input  ALU_OE,
  input  REG_A_WE,
  input  REG_B_WE,
  input  OR_OE,
  input  OR_WE,
  output [7:0] out_31,
  output [7:0] out_32,
  output [15:0] out_33,
  output [15:0] out_34,
  output [15:0] out_35,
  output [15:0] out_36,
  output [7:0] out_37,
  output [7:0] out_38,
  output [15:0] out_39,
  output [15:0] out_40,
  output [15:0] out_41,
  output [15:0] out_42,
  output [15:0] out_43
);

  wire clock_1_out, cu_v1_1_c0, cu_v1_1_c1, cu_v1_1_c2, cu_v1_1_c3, cu_v1_1_c4, cu_v1_1_c5, cu_v1_1_c6,
       cu_v1_1_c7, cu_v1_1_c8, cu_v1_1_c9, cu_v1_1_c10, cu_v1_1_c11, cu_v1_1_c12, cu_v1_1_c13, cu_v1_1_c14,
       cu_v1_1_c15, undriven;
  wire [2:0] counter_2_q;
  wire [3:0] counter_1_q;
  wire [7:0] MAR_dout;
  wire [15:0] bit_extender_1_out, bit_extender_2_out, ram_1_dout;
  wire [31:0] decimal_decoder16_1_dout, decimal_decoder16_2_dout, decimal_decoder16_3_dout,
       decimal_decoder16_4_dout, decimal_decoder16_5_dout;

  Clock clock_1 (.out(clock_1_out));
  Counter #(.max('h5), .width(4)) counter_1 (
    .count(cu_v1_1_c1), .clk(clock_1_out), .D(out_31[3:0]), .Q(counter_1_q));  // open: clr, load, up, carry
  assign bit_extender_1_out = {{12{counter_1_q[3]}}, counter_1_q};  // Bit_Extender bit_extender_1
  project_register_16 IR (
    .input_val(out_33), .WE(cu_v1_1_c7), .clk(clock_1_out), .reset(in_14), .OE(cu_v1_1_c8), .result(out_35),
    .Eight_LSB(out_31), .Eight_MSB(out_38));  // open: Dout
  project_register_16 RegA (
    .input_val(out_33), .WE(cu_v1_1_c12), .clk(clock_1_out), .reset(in_17), .OE(REG_A_OE), .result(out_40));  // open: Dout, Eight_LSB, Eight_MSB
  project_alu project_alu_1 (
    .A(out_40), .B(out_43), .AUSel(AUSel), .RUSel(RUSel), .OE(cu_v1_1_c11), .AUResult(out_42), .AUDout(out_33));  // open: RUResult
  assign out_31[3:0] = cu_v1_1_c0 ? counter_1_q : 4'bz;  // Controlled_Buffer controlled_buffer_1
  project_register_16 RegB (
    .input_val(out_33), .WE(cu_v1_1_c13), .clk(clock_1_out), .reset(in_22), .OE(in_23), .result(out_43));  // open: Dout, Eight_LSB, Eight_MSB
  Decimal_Decoder16 decimal_decoder16_1 (.Din(bit_extender_1_out), .Dout(decimal_decoder16_1_dout));
  _7_Segment_Display u_7_segment_display_1 (
    .g(decimal_decoder16_1_dout[15]), .f(decimal_decoder16_1_dout[14]), .a(decimal_decoder16_1_dout[13]),
    .b(decimal_decoder16_1_dout[12]), .e(decimal_decoder16_1_dout[31]), .d(decimal_decoder16_1_dout[30]),
    .c(decimal_decoder16_1_dout[29]), .dp(decimal_decoder16_1_dout[28]));
  _7_Segment_Display u_7_segment_display_2 (
    .g(decimal_decoder16_1_dout[11]), .f(decimal_decoder16_1_dout[10]), .a(decimal_decoder16_1_dout[9]),
    .b(decimal_decoder16_1_dout[8]), .e(decimal_decoder16_1_dout[27]), .d(decimal_decoder16_1_dout[26]),
    .c(decimal_decoder16_1_dout[25]), .dp(decimal_decoder16_1_dout[24]));
  Decimal_Decoder16 decimal_decoder16_2 (.Din(out_43), .Dout(decimal_decoder16_2_dout));
  _7_Segment_Display u_7_segment_display_3 (
    .g(decimal_decoder16_1_dout[7]), .f(decimal_decoder16_1_dout[6]), .a(decimal_decoder16_1_dout[5]),
    .b(decimal_decoder16_1_dout[4]), .e(decimal_decoder16_1_dout[23]), .d(decimal_decoder16_1_dout[22]),
    .c(decimal_decoder16_1_dout[21]), .dp(decimal_decoder16_1_dout[20]));
  _7_Segment_Display u_7_segment_display_4 (
    .g(decimal_decoder16_1_dout[3]), .f(decimal_decoder16_1_dout[2]), .a(decimal_decoder16_1_dout[1]),
    .b(decimal_decoder16_1_dout[0]), .e(decimal_decoder16_1_dout[19]), .d(decimal_decoder16_1_dout[18]),
    .c(decimal_decoder16_1_dout[17]), .dp(decimal_decoder16_1_dout[16]));
  Decimal_Decoder16 decimal_decoder16_3 (.Din(out_40), .Dout(decimal_decoder16_3_dout));
  _7_Segment_Display u_7_segment_display_5 (
    .g(decimal_decoder16_2_dout[15]), .f(decimal_decoder16_2_dout[14]), .a(decimal_decoder16_2_dout[13]),
    .b(decimal_decoder16_2_dout[12]), .e(decimal_decoder16_2_dout[31]), .d(decimal_decoder16_2_dout[30]),
    .c(decimal_decoder16_2_dout[29]), .dp(decimal_decoder16_2_dout[28]));
  _7_Segment_Display u_7_segment_display_6 (
    .g(decimal_decoder16_3_dout[15]), .f(decimal_decoder16_3_dout[14]), .a(decimal_decoder16_3_dout[13]),
    .b(decimal_decoder16_3_dout[12]), .e(decimal_decoder16_3_dout[31]), .d(decimal_decoder16_3_dout[30]),
    .c(decimal_decoder16_3_dout[29]), .dp(decimal_decoder16_3_dout[28]));
  _7_Segment_Display u_7_segment_display_7 (
    .g(decimal_decoder16_2_dout[11]), .f(decimal_decoder16_2_dout[10]), .a(decimal_decoder16_2_dout[9]),
    .b(decimal_decoder16_2_dout[8]), .e(decimal_decoder16_2_dout[27]), .d(decimal_decoder16_2_dout[26]),
    .c(decimal_decoder16_2_dout[25]), .dp(decimal_decoder16_2_dout[24]));
  _7_Segment_Display u_7_segment_display_8 (
    .g(decimal_decoder16_2_dout[7]), .f(decimal_decoder16_2_dout[6]), .a(decimal_decoder16_2_dout[5]),
    .b(decimal_decoder16_2_dout[4]), .e(decimal_decoder16_2_dout[23]), .d(decimal_decoder16_2_dout[22]),
    .c(decimal_decoder16_2_dout[21]), .dp(decimal_decoder16_2_dout[20]));
  _7_Segment_Display u_7_segment_display_9 (
    .g(decimal_decoder16_3_dout[11]), .f(decimal_decoder16_3_dout[10]), .a(decimal_decoder16_3_dout[9]),
    .b(decimal_decoder16_3_dout[8]), .e(decimal_decoder16_3_dout[27]), .d(decimal_decoder16_3_dout[26]),
    .c(decimal_decoder16_3_dout[25]), .dp(decimal_decoder16_3_dout[24]));
  _7_Segment_Display u_7_segment_display_10 (
    .g(decimal_decoder16_3_dout[7]), .f(decimal_decoder16_3_dout[6]), .a(decimal_decoder16_3_dout[5]),
    .b(decimal_decoder16_3_dout[4]), .e(decimal_decoder16_3_dout[23]), .d(decimal_decoder16_3_dout[22]),
    .c(decimal_decoder16_3_dout[21]), .dp(decimal_decoder16_3_dout[20]));
  _7_Segment_Display u_7_segment_display_11 (
    .g(decimal_decoder16_2_dout[3]), .f(decimal_decoder16_2_dout[2]), .a(decimal_decoder16_2_dout[1]),
    .b(decimal_decoder16_2_dout[0]), .e(decimal_decoder16_2_dout[19]), .d(decimal_decoder16_2_dout[18]),
    .c(decimal_decoder16_2_dout[17]), .dp(decimal_decoder16_2_dout[16]));
  _7_Segment_Display u_7_segment_display_12 (
    .g(decimal_decoder16_3_dout[3]), .f(decimal_decoder16_3_dout[2]), .a(decimal_decoder16_3_dout[1]),
    .b(decimal_decoder16_3_dout[0]), .e(decimal_decoder16_3_dout[19]), .d(decimal_decoder16_3_dout[18]),
    .c(decimal_decoder16_3_dout[17]), .dp(decimal_decoder16_3_dout[16]));
  assign out_33 = in_10 ? in_9 : 16'bz;  // Controlled_Buffer controlled_buffer_2
  assign out_33 = cu_v1_1_c5 ? out_34 : 16'bz;  // Controlled_Buffer controlled_buffer_3
  project_register_16 MBR (
    .input_val(out_33), .WE(cu_v1_1_c4), .clk(clock_1_out), .reset(in_12), .OE(cu_v1_1_c6), .result(out_34),
    .Dout(out_33));  // open: Eight_LSB, Eight_MSB
  project_register_8 MAR (
    .input_val(out_31), .WE(cu_v1_1_c9), .clk(clock_1_out), .reset(in_5), .OE(cu_v1_1_c10), .result(out_32),
    .Dout(MAR_dout));  // open: Eight_LSB, Eight_MSB
  project_register_16 OutReg (
    .input_val(out_33), .WE(cu_v1_1_c15), .clk(clock_1_out), .reset(in_19), .OE(cu_v1_1_c14),
    .result(out_41), .Dout(out_33));  // open: Eight_LSB, Eight_MSB
  Decimal_Decoder16 decimal_decoder16_4 (.Din(out_41), .Dout(decimal_decoder16_4_dout));
  _7_Segment_Display u_7_segment_display_13 (
    .g(decimal_decoder16_4_dout[15]), .f(decimal_decoder16_4_dout[14]), .a(decimal_decoder16_4_dout[13]),
    .b(decimal_decoder16_4_dout[12]), .e(decimal_decoder16_4_dout[31]), .d(decimal_decoder16_4_dout[30]),
    .c(decimal_decoder16_4_dout[29]), .dp(decimal_decoder16_4_dout[28]));
  _7_Segment_Display u_7_segment_display_14 (
    .g(decimal_decoder16_4_dout[11]), .f(decimal_decoder16_4_dout[10]), .a(decimal_decoder16_4_dout[9]),
    .b(decimal_decoder16_4_dout[8]), .e(decimal_decoder16_4_dout[27]), .d(decimal_decoder16_4_dout[26]),
    .c(decimal_decoder16_4_dout[25]), .dp(decimal_decoder16_4_dout[24]));
  _7_Segment_Display u_7_segment_display_15 (
    .g(decimal_decoder16_4_dout[7]), .f(decimal_decoder16_4_dout[6]), .a(decimal_decoder16_4_dout[5]),
    .b(decimal_decoder16_4_dout[4]), .e(decimal_decoder16_4_dout[23]), .d(decimal_decoder16_4_dout[22]),
    .c(decimal_decoder16_4_dout[21]), .dp(decimal_decoder16_4_dout[20]));
  _7_Segment_Display u_7_segment_display_16 (
    .g(decimal_decoder16_4_dout[3]), .f(decimal_decoder16_4_dout[2]), .a(decimal_decoder16_4_dout[1]),
    .b(decimal_decoder16_4_dout[0]), .e(decimal_decoder16_4_dout[19]), .d(decimal_decoder16_4_dout[18]),
    .c(decimal_decoder16_4_dout[17]), .dp(decimal_decoder16_4_dout[16]));
  assign MAR_dout = in_6 ? in_7 : 8'bz;  // Controlled_Buffer controlled_buffer_4
  assign out_33 = cu_v1_1_c3 ? ram_1_dout : 16'bz;  // Controlled_Buffer controlled_buffer_5
  RAM #(.dataWidth(16), .enables("line")) ram_1 (
    .addr(MAR_dout), .we(cu_v1_1_c2), .oe(undriven), .clk(clock_1_out), .din(out_33), .dout(ram_1_dout));
  Counter #(.max('h5), .width(3)) counter_2 (
    .clk(clock_1_out), .Q(counter_2_q));  // open: clr, load, up, count, D, carry
  assign bit_extender_2_out = {{13{counter_2_q[2]}}, counter_2_q};  // Bit_Extender bit_extender_2
  CU_v1 cu_v1_1 (
    .OPC7(out_38[7]), .OPC6(out_38[6]), .OPC5(out_38[5]), .OPC4(out_38[4]), .OPC3(out_38[3]),
    .OPC2(out_38[2]), .OPC1(out_38[1]), .OPC0(out_38[0]), .SC2(counter_2_q[2]), .SC1(counter_2_q[1]),
    .SC0(counter_2_q[0]), .C0(cu_v1_1_c0), .C1(cu_v1_1_c1), .C2(cu_v1_1_c2), .C3(cu_v1_1_c3),
    .C4(cu_v1_1_c4), .C5(cu_v1_1_c5), .C6(cu_v1_1_c6), .C7(cu_v1_1_c7), .C8(cu_v1_1_c8), .C9(cu_v1_1_c9),
    .C10(cu_v1_1_c10), .C11(cu_v1_1_c11), .C12(cu_v1_1_c12), .C13(cu_v1_1_c13), .C14(cu_v1_1_c14),
    .C15(cu_v1_1_c15));
  Decimal_Decoder16 decimal_decoder16_5 (
    .Din(bit_extender_2_out),
    .Dout({decimal_decoder16_5_dout[31:12], decimal_decoder16_5_dout[15:12], decimal_decoder16_5_dout[7:0]}));
  _7_Segment_Display u_7_segment_display_17 (
    .g(decimal_decoder16_5_dout[3]), .f(decimal_decoder16_5_dout[2]), .a(decimal_decoder16_5_dout[1]),
    .b(decimal_decoder16_5_dout[0]), .e(decimal_decoder16_5_dout[19]), .d(decimal_decoder16_5_dout[18]),
    .c(decimal_decoder16_5_dout[17]), .dp(decimal_decoder16_5_dout[16]));

  assign out_36 = out_33;
  assign out_37 = out_31;
  assign out_39 = out_33;
endmodule

module CU_v1 (
  input  OPC7,
  input  OPC6,
  input  OPC5,
  input  OPC4,
  input  OPC3,
  input  OPC2,
  input  OPC1,
  input  OPC0,
  input  SC2,
  input  SC1,
  input  SC0,
  output C0,
  output C1,
  output C2,
  output C3,
  output C4,
  output C5,
  output C6,
  output C7,
  output C8,
  output C9,
  output C10,
  output C11,
  output C12,
  output C13,
  output C14,
  output C15
);

  wire and_4_out, and_5_out, and_6_out, and_7_out, and_8_out, and_9_out, and_10_out, and_13_out, and_14_out,
       and_15_out, and_16_out, and_17_out, and_18_out, and_19_out, and_20_out, not_1_out, not_2_out,
       not_3_out, not_4_out, not_5_out;

  not not_1 (not_1_out, OPC1);
  not not_2 (not_2_out, OPC0);
  not not_3 (not_3_out, SC2);
  not not_4 (not_4_out, SC1);
  not not_5 (not_5_out, SC0);
  and and_1 (C0, not_3_out, not_4_out, not_5_out);
  and and_2 (C1, not_3_out, not_4_out, SC0);
  and and_3 (C2, OPC1, OPC0, SC2, not_4_out, not_5_out);
  and and_4 (and_4_out, not_3_out, not_4_out, SC0);
  and and_5 (and_5_out, not_1_out, SC2, not_4_out, not_5_out);
  and and_6 (and_6_out, not_3_out, not_4_out, SC0);
  and and_7 (and_7_out, not_1_out, SC2, not_4_out, not_5_out);
  and and_8 (and_8_out, OPC1, OPC0, not_3_out, SC0);
  and and_9 (and_9_out, not_3_out, SC1, not_5_out);
  and and_10 (and_10_out, not_1_out, SC2, not_4_out, SC0);
  and and_11 (C6, OPC1, OPC0, SC2, not_4_out, not_5_out);
  and and_12 (C7, not_3_out, SC1, not_5_out);
  and and_13 (and_13_out, not_1_out, not_3_out, SC1, SC0);
  and and_14 (and_14_out, OPC0, not_3_out, SC1, SC0);
  and and_15 (and_15_out, not_3_out, not_4_out, not_5_out);
  and and_16 (and_16_out, not_1_out, not_3_out, SC1, SC0);
  and and_17 (and_17_out, OPC0, not_3_out, SC1, SC0);
  and and_18 (and_18_out, not_3_out, not_4_out, SC0);
  and and_19 (and_19_out, not_1_out, SC2, not_4_out, not_5_out);
  and and_20 (and_20_out, OPC0, SC2, not_4_out, not_5_out);
  and and_21 (C11, OPC1, not_2_out, not_3_out, SC1, SC0);
  and and_22 (C12, not_1_out, not_2_out, SC2, not_4_out, SC0);
  and and_23 (C13, not_1_out, OPC0, SC2, not_4_out, SC0);
  and and_24 (C14, OPC1, OPC0, not_3_out, SC1, SC0);
  and and_25 (C15, OPC1, not_2_out, not_3_out, SC1, SC0);
  or or_1 (C3, and_4_out, and_5_out);
  or or_2 (C4, and_6_out, and_7_out, and_8_out);
  or or_3 (C5, and_9_out, and_10_out);
  or or_4 (C8, and_13_out, and_14_out);
  or or_5 (C9, and_15_out, and_16_out, and_17_out);
  or or_6 (C10, and_18_out, and_19_out, and_20_out);
endmodule

module Decimal_Decoder16 (
  input  [15:0] Din,
  output [31:0] Dout
);

  ROM #(.addrWidth(16), .dataWidth(32)) rom_1 (
    .addr(Din),
    .data({Dout[31:28], Dout[15:12], Dout[27:24], Dout[11:8], Dout[23:20], Dout[7:4], Dout[19:16], Dout[3:0]}));

  // Notes on the sheet:
  //   contents of rom_1 (hex, n*v repeats v):
  //   e7 21 cb 6b 2d 6e ee 23 ef 2f 21e7 2121 21cb 216b 212d 216e 21ee 2123 21ef 212f cbe7 cb21 cbcb cb6b
  //   cb2d cb6e cbee cb23 cbef cb2f 6be7 6b21 6bcb 6b6b 6b2d 6b6e 6bee 6b23 6bef 6b2f 2de7 2d21 2dcb 2d6b
  //   2d2d 2d6e 2dee 2d23 2def 2d2f 6ee7 6e21 6ecb 6e6b 6e2d 6e6e 6eee 6e23 6eef 6e2f eee7 ee21 eecb ee6b
  //   ee2d ee6e eeee ee23 eeef ee2f 23e7 2321 23cb 236b 232d 236e 23ee 2323 23ef 232f efe7 ef21 efcb ef6b
  //   ef2d ef6e efee ef23 efef ef2f 2fe7 2f21 2fcb 2f6b 2f2d 2f6e 2fee 2f23 2fef 2f2f 21e7e7 21e721 21e7cb
  //   21e76b 21e72d 21e76e 21e7ee 21e723 21e7ef 21e72f 2121e7 212121 2121cb 21216b 21212d 21216e 2121ee
  //   212123 2121ef 21212f 21cbe7 21cb21 21cbcb 21cb6b 21cb2d 21cb6e 21cbee 21cb23 21cbef 21cb2f 216be7
  //   216b21 216bcb 216b6b 216b2d 216b6e 216bee 216b23 216bef 216b2f 212de7 212d21 212dcb 212d6b 212d2d
  //   212d6e 212dee 212d23 212def 212d2f 216ee7 216e21 216ecb 216e6b 216e2d 216e6e 216eee 216e23 216eef
  //   216e2f 21eee7 21ee21 21eecb 21ee6b 21ee2d 21ee6e 21eeee 21ee23 21eeef 21ee2f 2123e7 212321 2123cb
  //   21236b 21232d 21236e 2123ee 212323 2123ef 21232f 21efe7 21ef21 21efcb 21ef6b 21ef2d 21ef6e 21efee
  //   21ef23 21efef 21ef2f 212fe7 212f21 212fcb 212f6b 212f2d 212f6e 212fee 212f23 212fef 212f2f cbe7e7
  //   cbe721 cbe7cb cbe76b cbe72d cbe76e cbe7ee cbe723 cbe7ef cbe72f cb21e7 cb2121 cb21cb cb216b cb212d
  //   cb216e cb21ee cb2123 cb21ef cb212f cbcbe7 cbcb21 cbcbcb cbcb6b cbcb2d cbcb6e cbcbee cbcb23 cbcbef
  //   cbcb2f cb6be7 cb6b21 cb6bcb cb6b6b cb6b2d cb6b6e cb6bee cb6b23 cb6bef cb6b2f cb2de7 cb2d21 cb2dcb
  //   cb2d6b cb2d2d cb2d6e cb2dee cb2d23 cb2def cb2d2f cb6ee7 cb6e21 cb6ecb cb6e6b cb6e2d cb6e6e
  //   Decimal Decoder
endmodule
