// Logisim project databus.circ as structural Verilog: 6 circuits, main circuit project_alu
module project_alu (
  input  [15:0] A,
  input  [15:0] B,
  input  [3:0] AUSel,
  input  [2:0] RUSel,
  input  OE,
  output [15:0] AUResult,
  output RUResult,
  output [15:0] AUDout
);

  project_ao project_ao_1 (.A(A), .B(B), .AUSel(AUSel), .AUResult(AUResult));
  project_ro project_ro_1 (.A(A), .B(B), .RUSel(RUSel), .RUResult(RUResult));
  assign AUDout = OE ? AUResult : 16'bz;  // Controlled_Buffer controlled_buffer_1
endmodule

module project_ao (
  input  [15:0] A,
  input  [15:0] B,
  input  [3:0] AUSel,
  output [15:0] AUResult
);

  wire [15:0] adder_1_out, and_1_out, divider_1_out, divider_1_rem, multiplier_1_out, negator_1_out,
       negator_2_out, or_1_out, shifter_1_out, shifter_2_out, shifter_3_out, shifter_4_out, subtractor_1_out,
       xor_1_out;

  Adder #(.width(16)) adder_1 (.a(A), .b(B), .out(adder_1_out));  // open: cin, cout
  assign and_1_out = A & B;  // AND_Gate and_1, 16 bits wide
  assign or_1_out = A | B;  // OR_Gate or_1, 16 bits wide
  assign xor_1_out = A ^ B;  // XOR_Gate xor_1, 16 bits wide
  Divider #(.width(16)) divider_1 (.a(A), .b(B), .out(divider_1_out), .rem(divider_1_rem));  // open: upper
  Multiplier #(.width(16)) multiplier_1 (.a(A), .b(B), .out(multiplier_1_out));  // open: cin, cout
  Subtractor #(.width(16)) subtractor_1 (.a(A), .b(B), .out(subtractor_1_out));  // open: bin, bout
  Shifter #(.width(16)) shifter_1 (.in(A), .\dist (4'b0010), .out(shifter_1_out));
  Shifter #(.width(16)) shifter_2 (.in(B), .\dist (4'b0010), .out(shifter_2_out));
  Shifter #(.shift("lr"), .width(16)) shifter_3 (.in(A), .\dist (4'b0010), .out(shifter_3_out));
  Shifter #(.shift("lr"), .width(16)) shifter_4 (.in(B), .\dist (4'b0010), .out(shifter_4_out));
  Negator #(.width(16)) negator_1 (.in(A), .out(negator_1_out));
  Negator #(.width(16)) negator_2 (.in(B), .out(negator_2_out));
  Multiplexer #(.select(4), .width(16)) multiplexer_1 (
    .in0(adder_1_out), .in1(and_1_out), .in2(or_1_out), .in3(xor_1_out), .in4(divider_1_out),
    .in5(divider_1_rem), .in6(multiplier_1_out), .in7(subtractor_1_out), .in8(shifter_1_out),
    .in9(shifter_2_out), .in10(shifter_3_out), .in11(shifter_4_out), .in12(negator_1_out),
    .in13(negator_2_out), .out(AUResult), .sel(AUSel));  // open: in14, in15
endmodule

module project_ro (
  input  [15:0] A,
  input  [15:0] B,
  input  [2:0] RUSel,
  output RUResult
);

  wire comparator_1_eq, comparator_1_gt, comparator_1_lt, not_1_out, or_1_out, or_2_out;

  or or_1 (or_1_out, comparator_1_gt, comparator_1_eq);
  Comparator #(.width(16)) comparator_1 (
    .a(A), .b(B), .gt(comparator_1_gt), .eq(comparator_1_eq), .lt(comparator_1_lt));
  or or_2 (or_2_out, comparator_1_lt, comparator_1_eq);
  not not_1 (not_1_out, comparator_1_eq);
  Multiplexer #(.select(3)) multiplexer_1 (
    .in0(comparator_1_gt), .in1(comparator_1_eq), .in2(or_1_out), .in3(comparator_1_lt), .in4(or_2_out),
    .in5(not_1_out), .out(RUResult), .sel(RUSel));  // open: in6, in7
endmodule

module project_register_16 (
  input  [15:0] input_val,
  input  WE,
  input  clk,
  input  reset,
  input  OE,
  output [15:0] result,
  output [15:0] Dout,
  output [7:0] Eight_LSB,
  output [7:0] Eight_MSB
);

  Register #(.width(16)) register_1 (.D(input_val), .en(WE), .clk(clk), .Q(result), .clr(reset));
  assign Dout = OE ? result : 16'bz;  // Controlled_Buffer controlled_buffer_1
  BitSelector #(.group(8), .width(16)) bitselector_1 (.in(Dout), .out(Eight_LSB), .sel(1'b0));
  BitSelector #(.group(8), .width(16)) bitselector_2 (.in(Dout), .out(Eight_MSB), .sel(1'b1));
endmodule

module project_register_8 (
  input  [7:0] input_val,
  input  WE,
  input  clk,
  input  reset,
  input  OE,
  output [7:0] result,
  output [7:0] Dout,
  output [3:0] Eight_LSB,
  output [3:0] Eight_MSB
);

  Register register_1 (.D(input_val), .en(WE), .clk(clk), .Q(result), .clr(reset));
  assign Dout = OE ? result : 8'bz;  // Controlled_Buffer controlled_buffer_1
  BitSelector #(.group(4)) bitselector_1 (.in(Dout), .out(Eight_LSB), .sel(1'b0));
  BitSelector #(.group(4)) bitselector_2 (.in(Dout), .out(Eight_MSB), .sel(1'b1));
endmodule

module Datapath (
  input  in_1,
  input  in_2,
  input  in_3,
  input  [15:0] in_4,
  input  in_5,
  input  in_6,
  input  in_7,
  input  in_8,
  input  in_9,
  input  in_10,
  input  in_11,
  input  in_12,
  input  in_13,
  input  in_14,
  input  in_15,
  input  in_16,
  input  in_17,
  input  in_18,
  input  [3:0] AUSel,
  input  [2:0] RUSel,
  input  in_21,
  input  in_22,
  input  in_23,
  input  in_24,
  input  CLK,
  output [7:0] out_26,
  output [15:0] out_27,
  output [15:0] out_28,
  output [15:0] out_29,
  output [15:0] out_30,
  output [15:0] out_31,
  output [15:0] out_32,
  output [15:0] out_33,
  output [15:0] out_34,
  output [15:0] out_35
);

  wire [7:0] IR_eight_lsb;

  project_register_16 IR (
    .input_val(out_27), .WE(in_10), .clk(CLK), .reset(in_11), .OE(in_12), .result(out_29),
    .Eight_LSB(IR_eight_lsb));  // open: Dout, Eight_MSB
  project_register_16 RegA (
    .input_val(out_27), .WE(in_13), .clk(CLK), .reset(in_14), .OE(in_15), .result(out_32));  // open: Dout, Eight_LSB, Eight_MSB
  project_alu project_alu_1 (
    .A(out_32), .B(out_35), .AUSel(AUSel), .RUSel(RUSel), .OE(in_21), .AUResult(out_34), .AUDout(out_27));  // open: RUResult
  project_register_16 RegB (
    .input_val(out_27), .WE(in_22), .clk(CLK), .reset(in_23), .OE(in_24), .result(out_35));  // open: Dout, Eight_LSB, Eight_MSB
  assign out_27 = in_5 ? in_4 : 16'bz;  // Controlled_Buffer controlled_buffer_1
  assign out_27 = in_6 ? out_28 : 16'bz;  // Controlled_Buffer controlled_buffer_2
  project_register_16 MBR (
    .input_val(out_27), .WE(in_7), .clk(CLK), .reset(in_8), .OE(in_9), .result(out_28), .Dout(out_27));  // open: Eight_LSB, Eight_MSB
  project_register_8 MAR (
    .input_val(IR_eight_lsb), .WE(in_1), .clk(CLK), .reset(in_2), .OE(in_3), .Dout(out_26));  // open: result, Eight_LSB, Eight_MSB
  project_register_16 OutReg (
    .input_val(out_27), .WE(in_16), .clk(CLK), .reset(in_17), .OE(in_18), .result(out_33), .Dout(out_27));  // open: Eight_LSB, Eight_MSB

  assign out_30 = out_27;
  assign out_31 = out_27;
endmodule
